// Logisim project 32bit_fp_display.circ as structural Verilog: 4 circuits, main circuit 32bit_decoder_10div
module _32bit_decoder_10div (
  input  [15:0] in,
  output [15:0] out,
  output [3:0] num_out
);

  wire [15:0] divider_1_rem;

  Divider #(.width(16)) divider_1 (.a(in), .b(16'ha), .out(out), .rem(divider_1_rem));  // open: upper
  Bit_Extender #(.in_width(16), .out_width(4)) bit_extender_1 (.in(divider_1_rem), .out(num_out));

  // Notes on the sheet:
  //   out: pull=down
  //   in: pull=down
  //   num_out: pull=down
endmodule

module _32bit_decoder_10mul (
  input  [15:0] in,
  output [15:0] out,
  output [3:0] num_out
);

  wire [15:4] multiplier_1_cout;

  Multiplier #(.width(16)) multiplier_1 (
    .a(in), .b(16'ha), .out(out), .cout({multiplier_1_cout, num_out}));  // open: cin
  Pull_Resistor pull_resistor_1 (.node(num_out));
endmodule

module _32bit_decoder (
  input  [31:0] in,
  output sign,
  output [3:0] _4,
  output [3:0] _1,
  output [3:0] _3,
  output [3:0] _2,
  output [3:0] _2_2,
  output [3:0] _3_2,
  output [3:0] _1_2,
  output [3:0] _4_2,
  output [3:0] _0,
  output [3:0] _5,
  output dot,
  output [3:0] _6,
  output [3:0] _7,
  output [3:0] _8,
  output [3:0] _9,
  output [3:0] _10,
  output [3:0] _11,
  output [3:0] _12,
  output [3:0] _13,
  output [3:0] _14,
  output [3:0] _15,
  output [3:0] _16
);

  wire [15:0] n32bit_decoder_10div_1_out, n32bit_decoder_10div_2_out, n32bit_decoder_10div_3_out,
       n32bit_decoder_10div_4_out, n32bit_decoder_10div_5_out, n32bit_decoder_10mul_1_out,
       n32bit_decoder_10mul_2_out, n32bit_decoder_10mul_3_out, n32bit_decoder_10mul_4_out,
       n32bit_decoder_10mul_5_out, n32bit_decoder_10mul_6_out, n32bit_decoder_10mul_7_out,
       n32bit_decoder_10mul_8_out, n32bit_decoder_10mul_9_out, n32bit_decoder_10mul_10_out,
       n32bit_decoder_10mul_11_out, n32bit_decoder_10mul_12_out, n32bit_decoder_10mul_13_out,
       n32bit_decoder_10mul_14_out, n32bit_decoder_10mul_15_out;
  wire [31:0] multiplexer_1_out, subtractor_1_out;

  _32bit_decoder_10div u_32bit_decoder_10div_1 (
    .in(n32bit_decoder_10div_4_out), .out(n32bit_decoder_10div_1_out), .num_out(_3));
  _32bit_decoder_10div u_32bit_decoder_10div_2 (
    .in(n32bit_decoder_10div_1_out), .out(n32bit_decoder_10div_2_out), .num_out(_4));
  Pull_Resistor pull_resistor_1 (.node(sign));
  BitSelector #(.width(32)) bitselector_1 (.in(in), .out(sign), .sel({5{1'b1}}));
  Pull_Resistor pull_resistor_2 (.node(in));
  _32bit_decoder_10div u_32bit_decoder_10div_3 (
    .in(n32bit_decoder_10div_5_out), .out(n32bit_decoder_10div_3_out), .num_out(_1_2));
  _32bit_decoder_10div u_32bit_decoder_10div_4 (
    .in(n32bit_decoder_10div_3_out), .out(n32bit_decoder_10div_4_out), .num_out(_2_2));
  Multiplexer #(.width(32)) multiplexer_1 (
    .in0(in), .in1(subtractor_1_out), .out(multiplexer_1_out), .sel(sign));  // open: en
  Subtractor #(.width(32)) subtractor_1 (.a({32{1'b0}}), .b(in), .out(subtractor_1_out));  // open: bin, bout
  _32bit_decoder_10div u_32bit_decoder_10div_5 (
    .in(multiplexer_1_out[31:16]), .out(n32bit_decoder_10div_5_out), .num_out(_0));
  _32bit_decoder_10mul u_32bit_decoder_10mul_1 (
    .in(multiplexer_1_out[15:0]), .out(n32bit_decoder_10mul_1_out), .num_out(_1));
  _32bit_decoder_10mul u_32bit_decoder_10mul_2 (
    .in(n32bit_decoder_10mul_1_out), .out(n32bit_decoder_10mul_2_out), .num_out(_2));
  _32bit_decoder_10mul u_32bit_decoder_10mul_3 (
    .in(n32bit_decoder_10mul_2_out), .out(n32bit_decoder_10mul_3_out), .num_out(_3_2));
  _32bit_decoder_10mul u_32bit_decoder_10mul_4 (
    .in(n32bit_decoder_10mul_5_out), .out(n32bit_decoder_10mul_4_out), .num_out(_5));
  _32bit_decoder_10mul u_32bit_decoder_10mul_5 (
    .in(n32bit_decoder_10mul_3_out), .out(n32bit_decoder_10mul_5_out), .num_out(_4_2));
  _32bit_decoder_10mul u_32bit_decoder_10mul_6 (
    .in(n32bit_decoder_10mul_7_out), .out(n32bit_decoder_10mul_6_out), .num_out(_7));
  _32bit_decoder_10mul u_32bit_decoder_10mul_7 (
    .in(n32bit_decoder_10mul_4_out), .out(n32bit_decoder_10mul_7_out), .num_out(_6));
  _32bit_decoder_10mul u_32bit_decoder_10mul_8 (
    .in(n32bit_decoder_10mul_6_out), .out(n32bit_decoder_10mul_8_out), .num_out(_8));
  _32bit_decoder_10mul u_32bit_decoder_10mul_9 (
    .in(n32bit_decoder_10mul_8_out), .out(n32bit_decoder_10mul_9_out), .num_out(_9));
  _32bit_decoder_10mul u_32bit_decoder_10mul_10 (
    .in(n32bit_decoder_10mul_9_out), .out(n32bit_decoder_10mul_10_out), .num_out(_10));
  _32bit_decoder_10mul u_32bit_decoder_10mul_11 (
    .in(n32bit_decoder_10mul_10_out), .out(n32bit_decoder_10mul_11_out), .num_out(_11));
  _32bit_decoder_10mul u_32bit_decoder_10mul_12 (
    .in(n32bit_decoder_10mul_13_out), .out(n32bit_decoder_10mul_12_out), .num_out(_13));
  _32bit_decoder_10mul u_32bit_decoder_10mul_13 (
    .in(n32bit_decoder_10mul_11_out), .out(n32bit_decoder_10mul_13_out), .num_out(_12));
  _32bit_decoder_10mul u_32bit_decoder_10mul_14 (
    .in(n32bit_decoder_10mul_12_out), .out(n32bit_decoder_10mul_14_out), .num_out(_14));
  _32bit_decoder_10mul u_32bit_decoder_10mul_15 (
    .in(n32bit_decoder_10mul_14_out), .out(n32bit_decoder_10mul_15_out), .num_out(_15));
  _32bit_decoder_10mul u_32bit_decoder_10mul_16 (.in(n32bit_decoder_10mul_15_out), .num_out(_16));  // open: out

  assign dot = 1'b1;

  // Other names for the same wires on the sheet: tunnel = sign

  // Notes on the sheet:
  //   _10: pull=down
  //   _1: pull=down
  //   _4_2: pull=down
  //   _3: pull=down
  //   _3_2: pull=down
  //   _14: pull=down
  //   _2_2: pull=down
  //   in: pull=down
  //   _16: pull=down
  //   _7: pull=down
  //   _12: pull=down
  //   _4: pull=down
  //   _13: pull=down
  //   _5: pull=down
  //   _2: pull=down
  //   _9: pull=down
  //   _11: pull=down
  //   _15: pull=down
  //   _8: pull=down
  //   _6: pull=down
  //   _1_2: pull=down
  //   _0: pull=down
endmodule

module _32bit_decoder_short (
  input  [31:0] in,
  output sign,
  output [3:0] _4,
  output [3:0] _1,
  output [3:0] _3,
  output [3:0] _2,
  output [3:0] _2_2,
  output [3:0] _3_2,
  output [3:0] _1_2,
  output [3:0] _4_2,
  output [3:0] _0,
  output [3:0] _5,
  output dot
);

  wire [15:0] n32bit_decoder_10div_1_out, n32bit_decoder_10div_3_out, n32bit_decoder_10div_4_out,
       n32bit_decoder_10div_5_out, n32bit_decoder_10mul_1_out, n32bit_decoder_10mul_2_out,
       n32bit_decoder_10mul_3_out, n32bit_decoder_10mul_5_out;
  wire [31:0] multiplexer_1_out, subtractor_1_out;

  _32bit_decoder_10div u_32bit_decoder_10div_1 (
    .in(n32bit_decoder_10div_4_out), .out(n32bit_decoder_10div_1_out), .num_out(_3));
  _32bit_decoder_10div u_32bit_decoder_10div_2 (.in(n32bit_decoder_10div_1_out), .num_out(_4));  // open: out
  Pull_Resistor pull_resistor_1 (.node(sign));
  BitSelector #(.width(32)) bitselector_1 (.in(in), .out(sign), .sel({5{1'b1}}));
  Pull_Resistor pull_resistor_2 (.node(in));
  _32bit_decoder_10div u_32bit_decoder_10div_3 (
    .in(n32bit_decoder_10div_5_out), .out(n32bit_decoder_10div_3_out), .num_out(_1_2));
  _32bit_decoder_10div u_32bit_decoder_10div_4 (
    .in(n32bit_decoder_10div_3_out), .out(n32bit_decoder_10div_4_out), .num_out(_2_2));
  Multiplexer #(.width(32)) multiplexer_1 (
    .in0(in), .in1(subtractor_1_out), .out(multiplexer_1_out), .sel(sign));  // open: en
  Subtractor #(.width(32)) subtractor_1 (.a({32{1'b0}}), .b(in), .out(subtractor_1_out));  // open: bin, bout
  _32bit_decoder_10div u_32bit_decoder_10div_5 (
    .in(multiplexer_1_out[31:16]), .out(n32bit_decoder_10div_5_out), .num_out(_0));
  _32bit_decoder_10mul u_32bit_decoder_10mul_1 (
    .in(multiplexer_1_out[15:0]), .out(n32bit_decoder_10mul_1_out), .num_out(_1));
  _32bit_decoder_10mul u_32bit_decoder_10mul_2 (
    .in(n32bit_decoder_10mul_1_out), .out(n32bit_decoder_10mul_2_out), .num_out(_2));
  _32bit_decoder_10mul u_32bit_decoder_10mul_3 (
    .in(n32bit_decoder_10mul_2_out), .out(n32bit_decoder_10mul_3_out), .num_out(_3_2));
  _32bit_decoder_10mul u_32bit_decoder_10mul_4 (.in(n32bit_decoder_10mul_5_out), .num_out(_5));  // open: out
  _32bit_decoder_10mul u_32bit_decoder_10mul_5 (
    .in(n32bit_decoder_10mul_3_out), .out(n32bit_decoder_10mul_5_out), .num_out(_4_2));

  assign dot = 1'b1;

  // Other names for the same wires on the sheet: tunnel = sign

  // Notes on the sheet:
  //   _1_2: pull=down
  //   _4: pull=down
  //   _2: pull=down
  //   _5: pull=down
  //   _3_2: pull=down
  //   in: pull=down
  //   _0: pull=down
  //   _3: pull=down
  //   _1: pull=down
  //   _4_2: pull=down
  //   _2_2: pull=down
endmodule
