// Logisim project fp_logic.circ as structural Verilog: 2 circuits, main circuit fp_mult
module fp_mult (
  input  [31:0] in1,
  input  [31:0] in2,
  output [31:0] out
);

  wire [31:0] multiplier_1_cout, multiplier_1_out, shifter_1_out, shifter_2_out;

  Multiplier #(.width(32)) multiplier_1 (
    .a(in1), .b(in2), .out(multiplier_1_out), .cout(multiplier_1_cout));  // open: cin
  Shifter #(.width(32), .shift("lr")) shifter_1 (.in(multiplier_1_out), .\dist (5'b10000), .out(shifter_1_out));
  Shifter #(.width(32)) shifter_2 (.in(multiplier_1_cout), .\dist (5'b10000), .out(shifter_2_out));
  Adder #(.width(32)) adder_1 (.a(shifter_1_out), .b(shifter_2_out), .out(out));  // open: cin, cout

  // Notes on the sheet:
  //   in2: pull=down
  //   out: pull=down
  //   in1: pull=down
  //   for now ignore
  //   TODO?: take care of carry (in both case the carry is out of 32bit bounds
endmodule

module fp_div (
  input  [31:0] in1,
  input  [31:0] in2,
  output [31:0] out
);

  wire xor_1_out;
  wire [31:0] adder_1_out, divider_1_out, divider_1_rem, divider_2_out, multiplexer_1_out, multiplexer_2_out,
       shifter_1_out, shifter_2_out, subtractor_1_out, subtractor_2_out, subtractor_3_out;

  Subtractor #(.width(32)) subtractor_1 (.a({32{1'b0}}), .b(in1), .out(subtractor_1_out));  // open: bin, bout
  Subtractor #(.width(32)) subtractor_2 (.a({32{1'b0}}), .b(in2), .out(subtractor_2_out));  // open: bin, bout
  Multiplexer #(.width(32)) multiplexer_1 (
    .in0(in1), .in1(subtractor_1_out), .out(multiplexer_1_out), .sel(in1[31]));  // open: en
  Multiplexer #(.width(32)) multiplexer_2 (
    .in0(in2), .in1(subtractor_2_out), .out(multiplexer_2_out), .sel(in2[31]));  // open: en
  xor xor_1 (xor_1_out, in2[31], in1[31]);
  Divider #(.width(32)) divider_1 (
    .a(multiplexer_1_out), .b(multiplexer_2_out), .out(divider_1_out), .rem(divider_1_rem));  // open: upper
  Shifter #(.width(32), .shift("lr")) shifter_1 (.in(multiplexer_2_out), .\dist (5'b10000), .out(shifter_1_out));
  Shifter #(.width(32)) shifter_2 (.in(divider_1_out), .\dist (5'b10000), .out(shifter_2_out));
  Adder #(.width(32)) adder_1 (.a(shifter_2_out), .b(divider_2_out), .out(adder_1_out));  // open: cin, cout
  Divider #(.width(32)) divider_2 (.a(divider_1_rem), .b(shifter_1_out), .out(divider_2_out));  // open: upper, rem
  Subtractor #(.width(32)) subtractor_3 (.a({32{1'b0}}), .b(adder_1_out), .out(subtractor_3_out));  // open: bin, bout
  Multiplexer #(.width(32)) multiplexer_3 (
    .in0(adder_1_out), .in1(subtractor_3_out), .out(out), .sel(xor_1_out));  // open: en

  // Notes on the sheet:
  //   in1: pull=down
  //   out: pull=down
  //   in2: pull=down
endmodule
