// Logisim project main.circ as structural Verilog: 5 circuits, main circuit main
module main (
  input  [31:0] in_1,
  input  [31:0] in_2,
  input  [5:0] x,
  input  [5:0] y,
  input  [31:0] Load_sample,
  input  state,
  input  Load_to_MR1,
  input  Load_to__MR2,
  input  [31:0] in_9,
  input  [31:0] in_10,
  input  [31:0] in_11,
  input  [31:0] in_12,
  input  [31:0] in_13,
  input  [31:0] in_14,
  input  [31:0] in_15,
  input  [31:0] in_16,
  input  [31:0] in_17
);

  wire and_1_out, button_1_out, clk, counter_1_carry, counter_2_carry, mission, n32bit_decoder_short_1_dot,
       n32bit_decoder_short_1_sign, n32bit_decoder_short_2_dot, n32bit_decoder_short_2_sign,
       n32bit_decoder_short_3_dot, n32bit_decoder_short_3_sign, n32bit_decoder_short_4_dot,
       n32bit_decoder_short_4_sign, n32bit_decoder_short_5_dot, n32bit_decoder_short_5_sign,
       n32bit_decoder_short_6_dot, n32bit_decoder_short_6_sign, n32bit_decoder_short_7_dot,
       n32bit_decoder_short_7_sign, n32bit_decoder_short_8_dot, n32bit_decoder_short_8_sign,
       n32bit_decoder_short_9_dot, n32bit_decoder_short_9_sign, n32bit_decoder_short_10_dot,
       n32bit_decoder_short_10_sign, n32bit_decoder_short_11_dot, n32bit_decoder_short_11_sign,
       n32bit_decoder_short_12_dot, n32bit_decoder_short_12_sign, n32bit_decoder_short_13_dot,
       n32bit_decoder_short_13_sign, n32bit_decoder_short_14_dot, n32bit_decoder_short_14_sign,
       n32bit_decoder_short_15_dot, n32bit_decoder_short_15_sign, n32bit_decoder_short_16_dot,
       n32bit_decoder_short_16_sign, n32bit_decoder_short_17_dot, n32bit_decoder_short_17_sign,
       n32bit_decoder_short_18_dot, n32bit_decoder_short_18_sign, n32bit_decoder_short_19_dot,
       n32bit_decoder_short_19_sign, n32bit_decoder_short_20_dot, n32bit_decoder_short_20_sign,
       n32bit_decoder_short_21_dot, n32bit_decoder_short_21_sign, n32bit_decoder_short_22_dot,
       n32bit_decoder_short_22_sign, reset_2_out, reset_out, update_out;
  wire [3:0] adder_1_out, bit_extender_2_out, bit_extender_3_out, matrix_addr_offset, matrix_addr_R1,
       matrix_addr_R2, n32bit_decoder_short_1__0, n32bit_decoder_short_1__1, n32bit_decoder_short_1__1_2,
       n32bit_decoder_short_1__2, n32bit_decoder_short_1__2_2, n32bit_decoder_short_1__3,
       n32bit_decoder_short_1__3_2, n32bit_decoder_short_1__4, n32bit_decoder_short_1__4_2,
       n32bit_decoder_short_1__5, n32bit_decoder_short_2__0, n32bit_decoder_short_2__1,
       n32bit_decoder_short_2__1_2, n32bit_decoder_short_2__2, n32bit_decoder_short_2__2_2,
       n32bit_decoder_short_2__3, n32bit_decoder_short_2__3_2, n32bit_decoder_short_2__4,
       n32bit_decoder_short_2__4_2, n32bit_decoder_short_2__5, n32bit_decoder_short_3__0,
       n32bit_decoder_short_3__1, n32bit_decoder_short_3__1_2, n32bit_decoder_short_3__2,
       n32bit_decoder_short_3__2_2, n32bit_decoder_short_3__3, n32bit_decoder_short_3__3_2,
       n32bit_decoder_short_3__4, n32bit_decoder_short_3__4_2, n32bit_decoder_short_3__5,
       n32bit_decoder_short_4__0, n32bit_decoder_short_4__1, n32bit_decoder_short_4__1_2,
       n32bit_decoder_short_4__2, n32bit_decoder_short_4__2_2, n32bit_decoder_short_4__3,
       n32bit_decoder_short_4__3_2, n32bit_decoder_short_4__4, n32bit_decoder_short_4__4_2,
       n32bit_decoder_short_4__5, n32bit_decoder_short_5__0, n32bit_decoder_short_5__1,
       n32bit_decoder_short_5__1_2, n32bit_decoder_short_5__2, n32bit_decoder_short_5__2_2,
       n32bit_decoder_short_5__3, n32bit_decoder_short_5__3_2, n32bit_decoder_short_5__4,
       n32bit_decoder_short_5__4_2, n32bit_decoder_short_5__5, n32bit_decoder_short_6__0,
       n32bit_decoder_short_6__1, n32bit_decoder_short_6__1_2, n32bit_decoder_short_6__2,
       n32bit_decoder_short_6__2_2, n32bit_decoder_short_6__3, n32bit_decoder_short_6__3_2,
       n32bit_decoder_short_6__4, n32bit_decoder_short_6__4_2, n32bit_decoder_short_6__5,
       n32bit_decoder_short_7__0, n32bit_decoder_short_7__1, n32bit_decoder_short_7__1_2,
       n32bit_decoder_short_7__2, n32bit_decoder_short_7__2_2, n32bit_decoder_short_7__3,
       n32bit_decoder_short_7__3_2, n32bit_decoder_short_7__4, n32bit_decoder_short_7__4_2,
       n32bit_decoder_short_7__5, n32bit_decoder_short_8__0, n32bit_decoder_short_8__1,
       n32bit_decoder_short_8__1_2, n32bit_decoder_short_8__2, n32bit_decoder_short_8__2_2,
       n32bit_decoder_short_8__3, n32bit_decoder_short_8__3_2, n32bit_decoder_short_8__4,
       n32bit_decoder_short_8__4_2, n32bit_decoder_short_8__5, n32bit_decoder_short_9__0,
       n32bit_decoder_short_9__1, n32bit_decoder_short_9__1_2, n32bit_decoder_short_9__2,
       n32bit_decoder_short_9__2_2, n32bit_decoder_short_9__3, n32bit_decoder_short_9__3_2,
       n32bit_decoder_short_9__4, n32bit_decoder_short_9__4_2, n32bit_decoder_short_9__5,
       n32bit_decoder_short_10__0, n32bit_decoder_short_10__1, n32bit_decoder_short_10__1_2,
       n32bit_decoder_short_10__2, n32bit_decoder_short_10__2_2, n32bit_decoder_short_10__3,
       n32bit_decoder_short_10__3_2, n32bit_decoder_short_10__4, n32bit_decoder_short_10__4_2,
       n32bit_decoder_short_10__5, n32bit_decoder_short_11__0, n32bit_decoder_short_11__1,
       n32bit_decoder_short_11__1_2, n32bit_decoder_short_11__2, n32bit_decoder_short_11__2_2,
       n32bit_decoder_short_11__3, n32bit_decoder_short_11__3_2, n32bit_decoder_short_11__4,
       n32bit_decoder_short_11__4_2, n32bit_decoder_short_11__5, n32bit_decoder_short_12__0,
       n32bit_decoder_short_12__1, n32bit_decoder_short_12__1_2, n32bit_decoder_short_12__2,
       n32bit_decoder_short_12__2_2, n32bit_decoder_short_12__3, n32bit_decoder_short_12__3_2,
       n32bit_decoder_short_12__4, n32bit_decoder_short_12__4_2, n32bit_decoder_short_12__5,
       n32bit_decoder_short_13__0, n32bit_decoder_short_13__1, n32bit_decoder_short_13__1_2,
       n32bit_decoder_short_13__2, n32bit_decoder_short_13__2_2, n32bit_decoder_short_13__3,
       n32bit_decoder_short_13__3_2, n32bit_decoder_short_13__4, n32bit_decoder_short_13__4_2,
       n32bit_decoder_short_13__5, n32bit_decoder_short_14__0, n32bit_decoder_short_14__1,
       n32bit_decoder_short_14__1_2, n32bit_decoder_short_14__2, n32bit_decoder_short_14__2_2,
       n32bit_decoder_short_14__3, n32bit_decoder_short_14__3_2, n32bit_decoder_short_14__4,
       n32bit_decoder_short_14__4_2, n32bit_decoder_short_14__5, n32bit_decoder_short_15__0,
       n32bit_decoder_short_15__1, n32bit_decoder_short_15__1_2, n32bit_decoder_short_15__2,
       n32bit_decoder_short_15__2_2, n32bit_decoder_short_15__3, n32bit_decoder_short_15__3_2,
       n32bit_decoder_short_15__4, n32bit_decoder_short_15__4_2, n32bit_decoder_short_15__5,
       n32bit_decoder_short_16__0, n32bit_decoder_short_16__1, n32bit_decoder_short_16__1_2,
       n32bit_decoder_short_16__2, n32bit_decoder_short_16__2_2, n32bit_decoder_short_16__3,
       n32bit_decoder_short_16__3_2, n32bit_decoder_short_16__4, n32bit_decoder_short_16__4_2,
       n32bit_decoder_short_16__5, n32bit_decoder_short_17__0, n32bit_decoder_short_17__1,
       n32bit_decoder_short_17__1_2, n32bit_decoder_short_17__2, n32bit_decoder_short_17__2_2,
       n32bit_decoder_short_17__3, n32bit_decoder_short_17__3_2, n32bit_decoder_short_17__4,
       n32bit_decoder_short_17__4_2, n32bit_decoder_short_17__5, n32bit_decoder_short_18__0,
       n32bit_decoder_short_18__1, n32bit_decoder_short_18__1_2, n32bit_decoder_short_18__2,
       n32bit_decoder_short_18__2_2, n32bit_decoder_short_18__3, n32bit_decoder_short_18__3_2,
       n32bit_decoder_short_18__4, n32bit_decoder_short_18__4_2, n32bit_decoder_short_18__5,
       n32bit_decoder_short_19__0, n32bit_decoder_short_19__1, n32bit_decoder_short_19__1_2,
       n32bit_decoder_short_19__2, n32bit_decoder_short_19__2_2, n32bit_decoder_short_19__3,
       n32bit_decoder_short_19__3_2, n32bit_decoder_short_19__4, n32bit_decoder_short_19__4_2,
       n32bit_decoder_short_19__5, n32bit_decoder_short_20__0, n32bit_decoder_short_20__1,
       n32bit_decoder_short_20__1_2, n32bit_decoder_short_20__2, n32bit_decoder_short_20__2_2,
       n32bit_decoder_short_20__3, n32bit_decoder_short_20__3_2, n32bit_decoder_short_20__4,
       n32bit_decoder_short_20__4_2, n32bit_decoder_short_20__5, n32bit_decoder_short_21__0,
       n32bit_decoder_short_21__1, n32bit_decoder_short_21__1_2, n32bit_decoder_short_21__2,
       n32bit_decoder_short_21__2_2, n32bit_decoder_short_21__3, n32bit_decoder_short_21__3_2,
       n32bit_decoder_short_21__4, n32bit_decoder_short_21__4_2, n32bit_decoder_short_21__5,
       n32bit_decoder_short_22__0, n32bit_decoder_short_22__1, n32bit_decoder_short_22__1_2,
       n32bit_decoder_short_22__2, n32bit_decoder_short_22__2_2, n32bit_decoder_short_22__3,
       n32bit_decoder_short_22__3_2, n32bit_decoder_short_22__4, n32bit_decoder_short_22__4_2,
       n32bit_decoder_short_22__5, pull_resistor_1_node;
  wire [23:0] bit_extender_1_out;
  wire [31:0] _11, _12, _13, _21, _22, _23, _31, _32, _33, adder_3_out, adder_4_out, adder_5_out, addr,
       bit_extender_4_out, dotmatrix_1_p1, dotmatrix_1_p2, f_aspect_ratio, f_fov_rad, fp_div_1_out,
       fp_div_4_out, fp_div_5_out, fp_div_6_out, fp_div_7_out, fp_div_8_out, fp_div_9_out, fp_div_10_out,
       fp_div_11_out, fp_mult_1_out, fp_mult_4_out, fp_mult_5_out, fp_mult_8_out, fp_mult_9_out,
       fp_mult_10_out, fp_mult_11_out, fp_mult_12_out, fp_mult_13_out, fp_mult_14_out, fp_round_1_out, h_2,
       matrix_mult_4x4_1_out11, matrix_mult_4x4_1_out12, matrix_mult_4x4_1_out13, matrix_mult_4x4_1_out14,
       matrix_mult_4x4_2_out11, matrix_mult_4x4_2_out12, matrix_mult_4x4_2_out13, matrix_mult_4x4_2_out14,
       matrix_mult_4x4_4_out11, matrix_mult_4x4_4_out12, matrix_mult_4x4_4_out13, matrix_mult_4x4_4_out14,
       matrix_reg_rev_1_out_11, matrix_reg_rev_1_out_12, matrix_reg_rev_1_out_13, matrix_reg_rev_1_out_21,
       matrix_reg_rev_1_out_22, matrix_reg_rev_1_out_23, matrix_reg_rev_1_out_31, matrix_reg_rev_1_out_32,
       matrix_reg_rev_1_out_33, matrix_reg_rev_2_out_11, matrix_reg_rev_2_out_12, matrix_reg_rev_2_out_13,
       matrix_reg_rev_2_out_21, matrix_reg_rev_2_out_22, matrix_reg_rev_2_out_23, matrix_reg_rev_2_out_31,
       matrix_reg_rev_2_out_32, matrix_reg_rev_2_out_33, n64x64_display_controller_1_x12,
       n64x64_display_controller_1_x21, n64x64_display_controller_1_x22, n64x64_display_controller_1_y12,
       n64x64_display_controller_1_y21, n64x64_display_controller_1_y22, negator_1_out, r, R1_11, R2_11,
       rom_1_data, sample_m_addr, sin_co_1_cos, sin_co_1_sin, subtractor_1_out, subtractor_2_out,
       subtractor_3_out, t, vec4_to_vec3_1_out1, vec4_to_vec3_1_out2, vec4_to_vec3_2_out1,
       vec4_to_vec3_2_out2, vec4_to_vec3_2_out3, vec4_to_vec3_3_out1, vec4_to_vec3_3_out2,
       vec4_to_vec3_3_out3, w_2;

  Clock clock_1 (.out(clk));
  Pull_Resistor pull_resistor_1 (.node(pull_resistor_1_node));
  Transistor #(.\type ("n"), .width(4)) transistor_1 (.in(4'b0101), .out(pull_resistor_1_node), .gate(mission));
  Adder #(.width(4)) adder_1 (.a(pull_resistor_1_node), .b(matrix_addr_offset), .out(adder_1_out));  // open: cin, cout
  Bit_Extender #(.in_width(32), .out_width(24)) bit_extender_1 (.in(addr), .out(bit_extender_1_out));
  Multiplier #(.width(32)) multiplier_1 (.a(Load_sample), .b(32'h30), .out(sample_m_addr));  // open: cin, cout
  // rising_edge_detector rising_edge_detector_1: pin names not known
  Button button_1 (.out(button_1_out));
  assign bit_extender_2_out = {{2{1'b0}}, matrix_addr_offset[1:0]};  // Bit_Extender bit_extender_2
  assign bit_extender_3_out = {{2{1'b0}}, matrix_addr_offset[3:2]};  // Bit_Extender bit_extender_3
  Transistor #(.\type ("n"), .width(4)) transistor_2 (.in(adder_1_out), .out(matrix_addr_R1), .gate(Load_to_MR1));
  Transistor #(.\type ("n"), .width(4)) transistor_3 (.in(adder_1_out), .out(matrix_addr_R2), .gate(Load_to__MR2));
  ROM #(.addrWidth(24), .dataWidth(32)) rom_1 (.addr(bit_extender_1_out), .data(rom_1_data));  // open: sel
  _7_Segment_Display u_7_segment_display_1 (.g(n32bit_decoder_short_1_sign));  // open: f, a, b, e, d, c, dp
  Hex_Digit_Display hex_digit_display_1 (.value(n32bit_decoder_short_1__4));  // open: dp
  fp_round fp_round_1 (.num(32'h8000), .rounding_number_eg__0_1__100_etc(32'h1999), .out(fp_round_1_out));
  _7_Segment_Display u_7_segment_display_2 (.g(n32bit_decoder_short_2_sign));  // open: f, a, b, e, d, c, dp
  Hex_Digit_Display hex_digit_display_2 (.value(n32bit_decoder_short_2__4));  // open: dp
  rising_edge_detector rising_edge_detector_2 (
    .signal(button_1_out), .clear(counter_2_carry), .sync(clk), .out(mission));
  and and_1 (and_1_out, mission, clk);
  assign bit_extender_4_out = {{24{1'b0}}, {bit_extender_3_out, bit_extender_2_out}};  // Bit_Extender bit_extender_4
  Pull_Resistor pull_resistor_2 (.node(R1_11));
  Transistor #(.\type ("n"), .width(32)) transistor_4 (.in(rom_1_data), .out(R1_11), .gate(Load_to_MR1));
  Pull_Resistor pull_resistor_3 (.node(R2_11));
  Transistor #(.\type ("n"), .width(32)) transistor_5 (.in(rom_1_data), .out(R2_11), .gate(Load_to__MR2));
  Hex_Digit_Display hex_digit_display_3 (.value(n32bit_decoder_short_1__3));  // open: dp
  Hex_Digit_Display hex_digit_display_4 (.value(n32bit_decoder_short_1__2_2));  // open: dp
  _7_Segment_Display u_7_segment_display_3 (.g(n32bit_decoder_short_3_sign));  // open: f, a, b, e, d, c, dp
  Hex_Digit_Display hex_digit_display_5 (.value(n32bit_decoder_short_3__4));  // open: dp
  Hex_Digit_Display hex_digit_display_6 (.value(n32bit_decoder_short_2__2_2));  // open: dp
  Hex_Digit_Display hex_digit_display_7 (.value(n32bit_decoder_short_2__3));  // open: dp
  Counter #(.width(2), .max('h3)) counter_1 (
    .Q(matrix_addr_offset[3:2]), .carry(counter_1_carry), .clk(and_1_out), .clr(counter_1_carry));  // open: load, D, count
  Counter #(.width(2), .max('h3)) counter_2 (
    .Q(matrix_addr_offset[1:0]), .carry(counter_2_carry), .clk(counter_1_carry), .clr(counter_2_carry));  // open: load, D, count
  Adder #(.width(32)) adder_2 (.a(bit_extender_4_out), .b(sample_m_addr), .out(addr));  // open: cin, cout
  Pull_Resistor pull_resistor_4 (.node(matrix_addr_R1));
  Pull_Resistor pull_resistor_5 (.node(matrix_addr_R2));
  Hex_Digit_Display hex_digit_display_8 (.value(n32bit_decoder_short_1__0), .dp(n32bit_decoder_short_1_dot));
  Hex_Digit_Display hex_digit_display_9 (.value(n32bit_decoder_short_1__1_2));  // open: dp
  Hex_Digit_Display hex_digit_display_10 (.value(n32bit_decoder_short_3__3));  // open: dp
  Hex_Digit_Display hex_digit_display_11 (.value(n32bit_decoder_short_3__2_2));  // open: dp
  Hex_Digit_Display hex_digit_display_12 (.value(n32bit_decoder_short_2__0), .dp(n32bit_decoder_short_2_dot));
  Hex_Digit_Display hex_digit_display_13 (.value(n32bit_decoder_short_2__1_2));  // open: dp
  _7_Segment_Display u_7_segment_display_4 (.g(n32bit_decoder_short_4_sign));  // open: f, a, b, e, d, c, dp
  _7_Segment_Display u_7_segment_display_5 (.g(n32bit_decoder_short_5_sign));  // open: f, a, b, e, d, c, dp
  _7_Segment_Display u_7_segment_display_6 (.g(n32bit_decoder_short_6_sign));  // open: f, a, b, e, d, c, dp
  Hex_Digit_Display hex_digit_display_14 (.value(n32bit_decoder_short_1__1));  // open: dp
  Hex_Digit_Display hex_digit_display_15 (.value(n32bit_decoder_short_1__2));  // open: dp
  Hex_Digit_Display hex_digit_display_16 (.value(n32bit_decoder_short_3__1_2));  // open: dp
  Hex_Digit_Display hex_digit_display_17 (.value(n32bit_decoder_short_3__0), .dp(n32bit_decoder_short_3_dot));
  Hex_Digit_Display hex_digit_display_18 (.value(n32bit_decoder_short_2__1));  // open: dp
  Hex_Digit_Display hex_digit_display_19 (.value(n32bit_decoder_short_2__2));  // open: dp
  fp_div fp_div_1 (.in1(32'h5a0000), .in2(32'h20000), .out(fp_div_1_out));
  Hex_Digit_Display hex_digit_display_20 (.value(n32bit_decoder_short_4__3));  // open: dp
  Hex_Digit_Display hex_digit_display_21 (.value(n32bit_decoder_short_4__4));  // open: dp
  Hex_Digit_Display hex_digit_display_22 (.value(n32bit_decoder_short_5__4));  // open: dp
  Hex_Digit_Display hex_digit_display_23 (.value(n32bit_decoder_short_5__3));  // open: dp
  Hex_Digit_Display hex_digit_display_24 (.value(n32bit_decoder_short_6__3));  // open: dp
  Hex_Digit_Display hex_digit_display_25 (.value(n32bit_decoder_short_6__4));  // open: dp
  Button reset (.out(reset_out));
  Hex_Digit_Display hex_digit_display_26 (.value(n32bit_decoder_short_1__3_2));  // open: dp
  Hex_Digit_Display hex_digit_display_27 (.value(n32bit_decoder_short_1__4_2));  // open: dp
  Hex_Digit_Display hex_digit_display_28 (.value(n32bit_decoder_short_3__1));  // open: dp
  Hex_Digit_Display hex_digit_display_29 (.value(n32bit_decoder_short_3__2));  // open: dp
  Hex_Digit_Display hex_digit_display_30 (.value(n32bit_decoder_short_2__3_2));  // open: dp
  Hex_Digit_Display hex_digit_display_31 (.value(n32bit_decoder_short_2__4_2));  // open: dp
  sin_co sin_co_1 (.in_1(fp_div_1_out), .sin(sin_co_1_sin), .cos(sin_co_1_cos));
  Hex_Digit_Display hex_digit_display_32 (.value(n32bit_decoder_short_4__1_2));  // open: dp
  Hex_Digit_Display hex_digit_display_33 (.value(n32bit_decoder_short_4__2_2));  // open: dp
  Hex_Digit_Display hex_digit_display_34 (.value(n32bit_decoder_short_5__1_2));  // open: dp
  Hex_Digit_Display hex_digit_display_35 (.value(n32bit_decoder_short_5__2_2));  // open: dp
  Hex_Digit_Display hex_digit_display_36 (.value(n32bit_decoder_short_6__2_2));  // open: dp
  Hex_Digit_Display hex_digit_display_37 (.value(n32bit_decoder_short_6__1_2));  // open: dp
  Hex_Digit_Display hex_digit_display_38 (.value(n32bit_decoder_short_1__5));  // open: dp
  _32bit_decoder_short u_32bit_decoder_short_1 (
    .sign(n32bit_decoder_short_1_sign), ._4(n32bit_decoder_short_1__4), ._3(n32bit_decoder_short_1__3),
    ._2_2(n32bit_decoder_short_1__2_2), ._1_2(n32bit_decoder_short_1__1_2), ._0(n32bit_decoder_short_1__0),
    .dot(n32bit_decoder_short_1_dot), .in(32'h8000), ._1(n32bit_decoder_short_1__1),
    ._2(n32bit_decoder_short_1__2), ._3_2(n32bit_decoder_short_1__3_2), ._4_2(n32bit_decoder_short_1__4_2),
    ._5(n32bit_decoder_short_1__5));
  Hex_Digit_Display hex_digit_display_39 (.value(n32bit_decoder_short_3__4_2));  // open: dp
  Hex_Digit_Display hex_digit_display_40 (.value(n32bit_decoder_short_3__3_2));  // open: dp
  Hex_Digit_Display hex_digit_display_41 (.value(n32bit_decoder_short_2__5));  // open: dp
  _32bit_decoder_short u_32bit_decoder_short_2 (
    .sign(n32bit_decoder_short_2_sign), ._4(n32bit_decoder_short_2__4), ._3(n32bit_decoder_short_2__3),
    ._2_2(n32bit_decoder_short_2__2_2), ._1_2(n32bit_decoder_short_2__1_2), ._0(n32bit_decoder_short_2__0),
    .dot(n32bit_decoder_short_2_dot), .in(32'h1999), ._1(n32bit_decoder_short_2__1),
    ._2(n32bit_decoder_short_2__2), ._3_2(n32bit_decoder_short_2__3_2), ._4_2(n32bit_decoder_short_2__4_2),
    ._5(n32bit_decoder_short_2__5));
  fp_div fp_div_2 (.in1(sin_co_1_cos), .in2(sin_co_1_sin), .out(f_fov_rad));
  Hex_Digit_Display hex_digit_display_42 (.value(n32bit_decoder_short_4__0), .dp(n32bit_decoder_short_4_dot));
  Hex_Digit_Display hex_digit_display_43 (.value(n32bit_decoder_short_4__1));  // open: dp
  Hex_Digit_Display hex_digit_display_44 (.value(n32bit_decoder_short_5__1));  // open: dp
  Hex_Digit_Display hex_digit_display_45 (.value(n32bit_decoder_short_5__0), .dp(n32bit_decoder_short_5_dot));
  Hex_Digit_Display hex_digit_display_46 (.value(n32bit_decoder_short_6__1));  // open: dp
  Hex_Digit_Display hex_digit_display_47 (.value(n32bit_decoder_short_6__0), .dp(n32bit_decoder_short_6_dot));
  Hex_Digit_Display hex_digit_display_48 (.value(n32bit_decoder_short_3__5));  // open: dp
  _32bit_decoder_short u_32bit_decoder_short_3 (
    .sign(n32bit_decoder_short_3_sign), ._4(n32bit_decoder_short_3__4), ._3(n32bit_decoder_short_3__3),
    ._2_2(n32bit_decoder_short_3__2_2), ._1_2(n32bit_decoder_short_3__1_2), ._0(n32bit_decoder_short_3__0),
    .dot(n32bit_decoder_short_3_dot), .in(fp_round_1_out), ._1(n32bit_decoder_short_3__1),
    ._2(n32bit_decoder_short_3__2), ._3_2(n32bit_decoder_short_3__3_2), ._4_2(n32bit_decoder_short_3__4_2),
    ._5(n32bit_decoder_short_3__5));
  _7_Segment_Display u_7_segment_display_7 (.g(n32bit_decoder_short_7_sign));  // open: f, a, b, e, d, c, dp
  Hex_Digit_Display hex_digit_display_49 (.value(n32bit_decoder_short_4__2));  // open: dp
  Hex_Digit_Display hex_digit_display_50 (.value(n32bit_decoder_short_4__3_2));  // open: dp
  Hex_Digit_Display hex_digit_display_51 (.value(n32bit_decoder_short_5__2));  // open: dp
  Hex_Digit_Display hex_digit_display_52 (.value(n32bit_decoder_short_5__3_2));  // open: dp
  Hex_Digit_Display hex_digit_display_53 (.value(n32bit_decoder_short_6__3_2));  // open: dp
  Hex_Digit_Display hex_digit_display_54 (.value(n32bit_decoder_short_6__2));  // open: dp
  matrix_reg_rev matrix_reg_rev_1 (
    .in_1(clk), .rst(reset_out), .in_11(R2_11), .in_21(R2_11), .in_31(R2_11), .in_12(R2_11), .in_22(R2_11),
    .in_32(R2_11), .in_13(R2_11), .in_23(R2_11), .in_33(R2_11), ._1__store_by_address_0__store_all(1'b1),
    .val___XXYY_address(matrix_addr_R2), .out_11(matrix_reg_rev_1_out_11), .out_21(matrix_reg_rev_1_out_21),
    .out_31(matrix_reg_rev_1_out_31), .out_12(matrix_reg_rev_1_out_12), .out_22(matrix_reg_rev_1_out_22),
    .out_32(matrix_reg_rev_1_out_32), .out_13(matrix_reg_rev_1_out_13), .out_23(matrix_reg_rev_1_out_23),
    .out_33(matrix_reg_rev_1_out_33));
  matrix_reg_rev matrix_reg_rev_2 (
    .in_1(clk), .rst(reset_out), .in_11(R1_11), .in_21(R1_11), .in_31(R1_11), .in_12(R1_11), .in_22(R1_11),
    .in_32(R1_11), .in_13(R1_11), .in_23(R1_11), .in_33(R1_11), ._1__store_by_address_0__store_all(1'b1),
    .val___XXYY_address(matrix_addr_R1), .out_11(matrix_reg_rev_2_out_11), .out_21(matrix_reg_rev_2_out_21),
    .out_31(matrix_reg_rev_2_out_31), .out_12(matrix_reg_rev_2_out_12), .out_22(matrix_reg_rev_2_out_22),
    .out_32(matrix_reg_rev_2_out_32), .out_13(matrix_reg_rev_2_out_13), .out_23(matrix_reg_rev_2_out_23),
    .out_33(matrix_reg_rev_2_out_33));
  Hex_Digit_Display hex_digit_display_55 (.value(n32bit_decoder_short_7__4));  // open: dp
  Hex_Digit_Display hex_digit_display_56 (.value(n32bit_decoder_short_4__4_2));  // open: dp
  Hex_Digit_Display hex_digit_display_57 (.value(n32bit_decoder_short_4__5));  // open: dp
  Hex_Digit_Display hex_digit_display_58 (.value(n32bit_decoder_short_5__4_2));  // open: dp
  Hex_Digit_Display hex_digit_display_59 (.value(n32bit_decoder_short_5__5));  // open: dp
  Hex_Digit_Display hex_digit_display_60 (.value(n32bit_decoder_short_6__4_2));  // open: dp
  Hex_Digit_Display hex_digit_display_61 (.value(n32bit_decoder_short_6__5));  // open: dp
  Hex_Digit_Display hex_digit_display_62 (.value(n32bit_decoder_short_7__2_2));  // open: dp
  Hex_Digit_Display hex_digit_display_63 (.value(n32bit_decoder_short_7__3));  // open: dp
  _7_Segment_Display u_7_segment_display_8 (.g(n32bit_decoder_short_8_sign));  // open: f, a, b, e, d, c, dp
  _32bit_decoder_short u_32bit_decoder_short_4 (
    .sign(n32bit_decoder_short_4_sign), ._4(n32bit_decoder_short_4__4), ._3(n32bit_decoder_short_4__3),
    ._2_2(n32bit_decoder_short_4__2_2), ._1_2(n32bit_decoder_short_4__1_2), ._0(n32bit_decoder_short_4__0),
    .dot(n32bit_decoder_short_4_dot), .in(_11), ._1(n32bit_decoder_short_4__1),
    ._2(n32bit_decoder_short_4__2), ._3_2(n32bit_decoder_short_4__3_2), ._4_2(n32bit_decoder_short_4__4_2),
    ._5(n32bit_decoder_short_4__5));
  _7_Segment_Display u_7_segment_display_9 (.g(n32bit_decoder_short_9_sign));  // open: f, a, b, e, d, c, dp
  _32bit_decoder_short u_32bit_decoder_short_5 (
    .sign(n32bit_decoder_short_5_sign), ._4(n32bit_decoder_short_5__4), ._3(n32bit_decoder_short_5__3),
    ._2_2(n32bit_decoder_short_5__2_2), ._1_2(n32bit_decoder_short_5__1_2), ._0(n32bit_decoder_short_5__0),
    .dot(n32bit_decoder_short_5_dot), .in(_12), ._1(n32bit_decoder_short_5__1),
    ._2(n32bit_decoder_short_5__2), ._3_2(n32bit_decoder_short_5__3_2), ._4_2(n32bit_decoder_short_5__4_2),
    ._5(n32bit_decoder_short_5__5));
  _7_Segment_Display u_7_segment_display_10 (.g(n32bit_decoder_short_10_sign));  // open: f, a, b, e, d, c, dp
  _32bit_decoder_short u_32bit_decoder_short_6 (
    .sign(n32bit_decoder_short_6_sign), ._4(n32bit_decoder_short_6__4), ._3(n32bit_decoder_short_6__3),
    ._2_2(n32bit_decoder_short_6__2_2), ._1_2(n32bit_decoder_short_6__1_2), ._0(n32bit_decoder_short_6__0),
    .dot(n32bit_decoder_short_6_dot), .in(_13), ._1(n32bit_decoder_short_6__1),
    ._2(n32bit_decoder_short_6__2), ._3_2(n32bit_decoder_short_6__3_2), ._4_2(n32bit_decoder_short_6__4_2),
    ._5(n32bit_decoder_short_6__5));
  matrix_mult matrix_mult_1 (
    .in_1(matrix_reg_rev_1_out_11), .in_2(matrix_reg_rev_1_out_21), .in_3(matrix_reg_rev_1_out_31),
    .in_4(matrix_reg_rev_1_out_12), .in_5(matrix_reg_rev_1_out_22), .in_6(matrix_reg_rev_1_out_32),
    .in_7(matrix_reg_rev_1_out_13), .in_8(matrix_reg_rev_1_out_23), .in_9(matrix_reg_rev_1_out_33),
    .in_10(matrix_reg_rev_2_out_11), .in_11(matrix_reg_rev_2_out_21), .in_12(matrix_reg_rev_2_out_31),
    .in_13(matrix_reg_rev_2_out_12), .in_14(matrix_reg_rev_2_out_22), .in_15(matrix_reg_rev_2_out_32),
    .in_16(matrix_reg_rev_2_out_13), .in_17(matrix_reg_rev_2_out_23), .in_18(matrix_reg_rev_2_out_33),
    .out11(_11), .out21(_21), .out31(_31), .out12(_12), .out22(_22), .out32(_32), .out13(_13), .out23(_23),
    .out33(_33));
  Hex_Digit_Display hex_digit_display_64 (.value(n32bit_decoder_short_7__0), .dp(n32bit_decoder_short_7_dot));
  Hex_Digit_Display hex_digit_display_65 (.value(n32bit_decoder_short_7__1_2));  // open: dp
  fp_mult fp_mult_1 (.in1(32'h1999), .in2(32'h3e80000), .out(fp_mult_1_out));
  Hex_Digit_Display hex_digit_display_66 (.value(n32bit_decoder_short_8__4));  // open: dp
  Hex_Digit_Display hex_digit_display_67 (.value(n32bit_decoder_short_9__4));  // open: dp
  Hex_Digit_Display hex_digit_display_68 (.value(n32bit_decoder_short_10__4));  // open: dp
  _7_Segment_Display u_7_segment_display_11 (.g(n32bit_decoder_short_11_sign));  // open: f, a, b, e, d, c, dp
  Hex_Digit_Display hex_digit_display_69 (.value(n32bit_decoder_short_11__4));  // open: dp
  fp_mult fp_mult_2 (.in1(32'h400000), .in2(32'h8000), .out(h_2));
  fp_mult fp_mult_3 (.in1(32'h400000), .in2(32'h8000), .out(w_2));
  fp_div fp_div_3 (.in1(32'h400000), .in2(32'h400000), .out(f_aspect_ratio));
  Hex_Digit_Display hex_digit_display_70 (.value(n32bit_decoder_short_7__2));  // open: dp
  Hex_Digit_Display hex_digit_display_71 (.value(n32bit_decoder_short_7__1));  // open: dp
  Adder #(.width(32)) adder_3 (.a(32'h3e80000), .b(32'h1999), .out(adder_3_out));  // open: cin, cout
  Subtractor #(.width(32)) subtractor_1 (.a(32'h1999), .b(32'h3e80000), .out(subtractor_1_out));  // open: bin, bout
  fp_mult fp_mult_4 (.in1(fp_mult_1_out), .in2(32'h20000), .out(fp_mult_4_out));
  Hex_Digit_Display hex_digit_display_72 (.value(n32bit_decoder_short_8__3));  // open: dp
  Hex_Digit_Display hex_digit_display_73 (.value(n32bit_decoder_short_8__2_2));  // open: dp
  Hex_Digit_Display hex_digit_display_74 (.value(n32bit_decoder_short_9__2_2));  // open: dp
  Hex_Digit_Display hex_digit_display_75 (.value(n32bit_decoder_short_9__3));  // open: dp
  Hex_Digit_Display hex_digit_display_76 (.value(n32bit_decoder_short_10__2_2));  // open: dp
  Hex_Digit_Display hex_digit_display_77 (.value(n32bit_decoder_short_10__3));  // open: dp
  Hex_Digit_Display hex_digit_display_78 (.value(n32bit_decoder_short_11__3));  // open: dp
  Hex_Digit_Display hex_digit_display_79 (.value(n32bit_decoder_short_11__2_2));  // open: dp
  fp_mult fp_mult_5 (.in1(32'h3e80000), .in2(32'hffff0000), .out(fp_mult_5_out));
  Hex_Digit_Display hex_digit_display_80 (.value(n32bit_decoder_short_7__4_2));  // open: dp
  Hex_Digit_Display hex_digit_display_81 (.value(n32bit_decoder_short_7__3_2));  // open: dp
  fp_mult fp_mult_6 (.in1(32'h400000), .in2(32'h8000), .out(t));
  fp_mult fp_mult_7 (.in1(32'h400000), .in2(32'h8000), .out(r));
  fp_div fp_div_4 (.in1(32'h1999), .in2(r), .out(fp_div_4_out));
  fp_div fp_div_5 (.in1(32'h1999), .in2(t), .out(fp_div_5_out));
  fp_div fp_div_6 (.in1(adder_3_out), .in2(subtractor_1_out), .out(fp_div_6_out));
  fp_div fp_div_7 (.in1(fp_mult_4_out), .in2(subtractor_1_out), .out(fp_div_7_out));
  Hex_Digit_Display hex_digit_display_82 (.value(n32bit_decoder_short_8__0), .dp(n32bit_decoder_short_8_dot));
  Hex_Digit_Display hex_digit_display_83 (.value(n32bit_decoder_short_8__1_2));  // open: dp
  Hex_Digit_Display hex_digit_display_84 (.value(n32bit_decoder_short_9__1_2));  // open: dp
  Hex_Digit_Display hex_digit_display_85 (.value(n32bit_decoder_short_9__0), .dp(n32bit_decoder_short_9_dot));
  Hex_Digit_Display hex_digit_display_86 (.value(n32bit_decoder_short_10__0), .dp(n32bit_decoder_short_10_dot));
  Hex_Digit_Display hex_digit_display_87 (.value(n32bit_decoder_short_10__1_2));  // open: dp
  Hex_Digit_Display hex_digit_display_88 (.value(n32bit_decoder_short_11__0), .dp(n32bit_decoder_short_11_dot));
  Hex_Digit_Display hex_digit_display_89 (.value(n32bit_decoder_short_11__1_2));  // open: dp
  fp_mult fp_mult_8 (.in1(f_aspect_ratio), .in2(f_fov_rad), .out(fp_mult_8_out));
  fp_mult fp_mult_9 (.in1(fp_mult_5_out), .in2(32'h1999), .out(fp_mult_9_out));
  fp_div fp_div_8 (.in1(fp_mult_9_out), .in2(subtractor_2_out), .out(fp_div_8_out));
  fp_div fp_div_9 (.in1(32'h3e80000), .in2(subtractor_2_out), .out(fp_div_9_out));
  Subtractor #(.width(32)) subtractor_2 (.a(32'h3e80000), .b(32'h1999), .out(subtractor_2_out));  // open: bin, bout
  Hex_Digit_Display hex_digit_display_90 (.value(n32bit_decoder_short_7__5));  // open: dp
  _32bit_decoder_short u_32bit_decoder_short_7 (
    .sign(n32bit_decoder_short_7_sign), ._4(n32bit_decoder_short_7__4), ._3(n32bit_decoder_short_7__3),
    ._2_2(n32bit_decoder_short_7__2_2), ._1_2(n32bit_decoder_short_7__1_2), ._0(n32bit_decoder_short_7__0),
    .dot(n32bit_decoder_short_7_dot), .in(f_fov_rad), ._1(n32bit_decoder_short_7__1),
    ._2(n32bit_decoder_short_7__2), ._3_2(n32bit_decoder_short_7__3_2), ._4_2(n32bit_decoder_short_7__4_2),
    ._5(n32bit_decoder_short_7__5));
  Hex_Digit_Display hex_digit_display_91 (.value(n32bit_decoder_short_8__2));  // open: dp
  Hex_Digit_Display hex_digit_display_92 (.value(n32bit_decoder_short_8__1));  // open: dp
  Hex_Digit_Display hex_digit_display_93 (.value(n32bit_decoder_short_9__1));  // open: dp
  Hex_Digit_Display hex_digit_display_94 (.value(n32bit_decoder_short_9__2));  // open: dp
  Hex_Digit_Display hex_digit_display_95 (.value(n32bit_decoder_short_10__2));  // open: dp
  Hex_Digit_Display hex_digit_display_96 (.value(n32bit_decoder_short_10__1));  // open: dp
  Hex_Digit_Display hex_digit_display_97 (.value(n32bit_decoder_short_11__2));  // open: dp
  Hex_Digit_Display hex_digit_display_98 (.value(n32bit_decoder_short_11__1));  // open: dp
  _7_Segment_Display u_7_segment_display_12 (.g(n32bit_decoder_short_12_sign));  // open: f, a, b, e, d, c, dp
  Hex_Digit_Display hex_digit_display_99 (.value(n32bit_decoder_short_8__3_2));  // open: dp
  Hex_Digit_Display hex_digit_display_100 (.value(n32bit_decoder_short_8__4_2));  // open: dp
  Hex_Digit_Display hex_digit_display_101 (.value(n32bit_decoder_short_9__3_2));  // open: dp
  Hex_Digit_Display hex_digit_display_102 (.value(n32bit_decoder_short_9__4_2));  // open: dp
  Hex_Digit_Display hex_digit_display_103 (.value(n32bit_decoder_short_10__4_2));  // open: dp
  Hex_Digit_Display hex_digit_display_104 (.value(n32bit_decoder_short_10__3_2));  // open: dp
  Hex_Digit_Display hex_digit_display_105 (.value(n32bit_decoder_short_11__3_2));  // open: dp
  Hex_Digit_Display hex_digit_display_106 (.value(n32bit_decoder_short_11__4_2));  // open: dp
  Hex_Digit_Display hex_digit_display_107 (.value(n32bit_decoder_short_12__3));  // open: dp
  Hex_Digit_Display hex_digit_display_108 (.value(n32bit_decoder_short_12__4));  // open: dp
  Hex_Digit_Display hex_digit_display_109 (.value(n32bit_decoder_short_8__5));  // open: dp
  _32bit_decoder_short u_32bit_decoder_short_8 (
    .sign(n32bit_decoder_short_8_sign), ._4(n32bit_decoder_short_8__4), ._3(n32bit_decoder_short_8__3),
    ._2_2(n32bit_decoder_short_8__2_2), ._1_2(n32bit_decoder_short_8__1_2), ._0(n32bit_decoder_short_8__0),
    .dot(n32bit_decoder_short_8_dot), .in(_21), ._1(n32bit_decoder_short_8__1),
    ._2(n32bit_decoder_short_8__2), ._3_2(n32bit_decoder_short_8__3_2), ._4_2(n32bit_decoder_short_8__4_2),
    ._5(n32bit_decoder_short_8__5));
  Hex_Digit_Display hex_digit_display_110 (.value(n32bit_decoder_short_9__5));  // open: dp
  _32bit_decoder_short u_32bit_decoder_short_9 (
    .sign(n32bit_decoder_short_9_sign), ._4(n32bit_decoder_short_9__4), ._3(n32bit_decoder_short_9__3),
    ._2_2(n32bit_decoder_short_9__2_2), ._1_2(n32bit_decoder_short_9__1_2), ._0(n32bit_decoder_short_9__0),
    .dot(n32bit_decoder_short_9_dot), .in(_22), ._1(n32bit_decoder_short_9__1),
    ._2(n32bit_decoder_short_9__2), ._3_2(n32bit_decoder_short_9__3_2), ._4_2(n32bit_decoder_short_9__4_2),
    ._5(n32bit_decoder_short_9__5));
  Hex_Digit_Display hex_digit_display_111 (.value(n32bit_decoder_short_10__5));  // open: dp
  _32bit_decoder_short u_32bit_decoder_short_10 (
    .sign(n32bit_decoder_short_10_sign), ._4(n32bit_decoder_short_10__4), ._3(n32bit_decoder_short_10__3),
    ._2_2(n32bit_decoder_short_10__2_2), ._1_2(n32bit_decoder_short_10__1_2),
    ._0(n32bit_decoder_short_10__0), .dot(n32bit_decoder_short_10_dot), .in(_23),
    ._1(n32bit_decoder_short_10__1), ._2(n32bit_decoder_short_10__2), ._3_2(n32bit_decoder_short_10__3_2),
    ._4_2(n32bit_decoder_short_10__4_2), ._5(n32bit_decoder_short_10__5));
  Hex_Digit_Display hex_digit_display_112 (.value(n32bit_decoder_short_11__5));  // open: dp
  _32bit_decoder_short u_32bit_decoder_short_11 (
    .sign(n32bit_decoder_short_11_sign), ._4(n32bit_decoder_short_11__4), ._3(n32bit_decoder_short_11__3),
    ._2_2(n32bit_decoder_short_11__2_2), ._1_2(n32bit_decoder_short_11__1_2),
    ._0(n32bit_decoder_short_11__0), .dot(n32bit_decoder_short_11_dot), .in(in_2),
    ._1(n32bit_decoder_short_11__1), ._2(n32bit_decoder_short_11__2), ._3_2(n32bit_decoder_short_11__3_2),
    ._4_2(n32bit_decoder_short_11__4_2), ._5(n32bit_decoder_short_11__5));
  Hex_Digit_Display hex_digit_display_113 (.value(n32bit_decoder_short_12__2_2));  // open: dp
  Hex_Digit_Display hex_digit_display_114 (.value(n32bit_decoder_short_12__1_2));  // open: dp
  _7_Segment_Display u_7_segment_display_13 (.g(n32bit_decoder_short_13_sign));  // open: f, a, b, e, d, c, dp
  _7_Segment_Display u_7_segment_display_14 (.g(n32bit_decoder_short_14_sign));  // open: f, a, b, e, d, c, dp
  _7_Segment_Display u_7_segment_display_15 (.g(n32bit_decoder_short_15_sign));  // open: f, a, b, e, d, c, dp
  Hex_Digit_Display hex_digit_display_115 (.value(n32bit_decoder_short_12__1));  // open: dp
  Hex_Digit_Display hex_digit_display_116 (.value(n32bit_decoder_short_12__0), .dp(n32bit_decoder_short_12_dot));
  Hex_Digit_Display hex_digit_display_117 (.value(n32bit_decoder_short_13__3));  // open: dp
  Hex_Digit_Display hex_digit_display_118 (.value(n32bit_decoder_short_13__4));  // open: dp
  Hex_Digit_Display hex_digit_display_119 (.value(n32bit_decoder_short_14__4));  // open: dp
  Hex_Digit_Display hex_digit_display_120 (.value(n32bit_decoder_short_14__3));  // open: dp
  Hex_Digit_Display hex_digit_display_121 (.value(n32bit_decoder_short_15__3));  // open: dp
  Hex_Digit_Display hex_digit_display_122 (.value(n32bit_decoder_short_15__4));  // open: dp
  Hex_Digit_Display hex_digit_display_123 (.value(n32bit_decoder_short_12__2));  // open: dp
  Hex_Digit_Display hex_digit_display_124 (.value(n32bit_decoder_short_12__3_2));  // open: dp
  matrix_mult_4x4 matrix_mult_4x4_1 (
    .in_1(in_9), .in_5(in_10), .in_9(in_11), .in_13(32'h10000), .in_17(fp_mult_8_out), .in_22(f_fov_rad),
    .in_27(fp_div_8_out), .in_28(fp_div_9_out), .in_31(32'h10000), .out11(matrix_mult_4x4_1_out11),
    .out12(matrix_mult_4x4_1_out12), .out13(matrix_mult_4x4_1_out13), .out14(matrix_mult_4x4_1_out14));  // open: in_2, in_3, in_4, in_6, in_7, in_8, in_10, in_11, in_12, in_14, in_15, in_16, in_18, in_19, in_20, in_21, in_23, in_24, in_25, in_26, in_29, in_30, in_32, out21, out31, out41, out22, out32, out42, out23, out33, out43, out24, out34, out44
  matrix_mult_4x4 matrix_mult_4x4_2 (
    .in_1(in_12), .in_5(in_14), .in_9(in_16), .in_13(32'h10000), .in_17(fp_div_4_out), .in_21(fp_div_4_out),
    .in_22(fp_div_5_out), .in_27(fp_div_6_out), .in_28(fp_div_7_out), .in_31(32'hffff0000),
    .out11(matrix_mult_4x4_2_out11), .out12(matrix_mult_4x4_2_out12), .out13(matrix_mult_4x4_2_out13),
    .out14(matrix_mult_4x4_2_out14));  // open: in_2, in_3, in_4, in_6, in_7, in_8, in_10, in_11, in_12, in_14, in_15, in_16, in_18, in_19, in_20, in_23, in_24, in_25, in_26, in_29, in_30, in_32, out21, out31, out41, out22, out32, out42, out23, out33, out43, out24, out34, out44
  Hex_Digit_Display hex_digit_display_125 (.value(n32bit_decoder_short_13__2_2));  // open: dp
  Hex_Digit_Display hex_digit_display_126 (.value(n32bit_decoder_short_13__1_2));  // open: dp
  Hex_Digit_Display hex_digit_display_127 (.value(n32bit_decoder_short_14__2_2));  // open: dp
  Hex_Digit_Display hex_digit_display_128 (.value(n32bit_decoder_short_14__1_2));  // open: dp
  Hex_Digit_Display hex_digit_display_129 (.value(n32bit_decoder_short_15__1_2));  // open: dp
  Hex_Digit_Display hex_digit_display_130 (.value(n32bit_decoder_short_15__2_2));  // open: dp
  Button update (.out(update_out));
  Button reset_2 (.out(reset_2_out));
  Hex_Digit_Display hex_digit_display_131 (.value(n32bit_decoder_short_12__4_2));  // open: dp
  Hex_Digit_Display hex_digit_display_132 (.value(n32bit_decoder_short_12__5));  // open: dp
  _32bit_decoder_short u_32bit_decoder_short_12 (
    .sign(n32bit_decoder_short_12_sign), ._4(n32bit_decoder_short_12__4), ._3(n32bit_decoder_short_12__3),
    ._2_2(n32bit_decoder_short_12__2_2), ._1_2(n32bit_decoder_short_12__1_2),
    ._0(n32bit_decoder_short_12__0), .dot(n32bit_decoder_short_12_dot), .in(in_9),
    ._1(n32bit_decoder_short_12__1), ._2(n32bit_decoder_short_12__2), ._3_2(n32bit_decoder_short_12__3_2),
    ._4_2(n32bit_decoder_short_12__4_2), ._5(n32bit_decoder_short_12__5));
  vec4_to_vec3 vec4_to_vec3_1 (
    .in1(matrix_mult_4x4_2_out11), .in2(matrix_mult_4x4_2_out12), .in3(matrix_mult_4x4_2_out13),
    .in4(matrix_mult_4x4_2_out14), .out1(vec4_to_vec3_1_out1), .out2(vec4_to_vec3_1_out2));  // open: out3
  Hex_Digit_Display hex_digit_display_133 (.value(n32bit_decoder_short_13__1));  // open: dp
  Hex_Digit_Display hex_digit_display_134 (.value(n32bit_decoder_short_13__0), .dp(n32bit_decoder_short_13_dot));
  Hex_Digit_Display hex_digit_display_135 (.value(n32bit_decoder_short_14__0), .dp(n32bit_decoder_short_14_dot));
  Hex_Digit_Display hex_digit_display_136 (.value(n32bit_decoder_short_14__1));  // open: dp
  Hex_Digit_Display hex_digit_display_137 (.value(n32bit_decoder_short_15__0), .dp(n32bit_decoder_short_15_dot));
  Hex_Digit_Display hex_digit_display_138 (.value(n32bit_decoder_short_15__1));  // open: dp
  vec4_to_vec3 vec4_to_vec3_2 (
    .in1(matrix_mult_4x4_1_out11), .in2(matrix_mult_4x4_1_out12), .in3(matrix_mult_4x4_1_out13),
    .in4(matrix_mult_4x4_1_out14), .out1(vec4_to_vec3_2_out1), .out2(vec4_to_vec3_2_out2),
    .out3(vec4_to_vec3_2_out3));
  Adder #(.width(32)) adder_4 (.a(32'h10000), .b(vec4_to_vec3_1_out1), .out(adder_4_out));  // open: cin, cout
  Adder #(.width(32)) adder_5 (.a(vec4_to_vec3_1_out2), .b(32'h10000), .out(adder_5_out));  // open: cin, cout
  Hex_Digit_Display hex_digit_display_139 (.value(n32bit_decoder_short_13__3_2));  // open: dp
  Hex_Digit_Display hex_digit_display_140 (.value(n32bit_decoder_short_13__2));  // open: dp
  Hex_Digit_Display hex_digit_display_141 (.value(n32bit_decoder_short_14__3_2));  // open: dp
  Hex_Digit_Display hex_digit_display_142 (.value(n32bit_decoder_short_14__2));  // open: dp
  Hex_Digit_Display hex_digit_display_143 (.value(n32bit_decoder_short_15__3_2));  // open: dp
  Hex_Digit_Display hex_digit_display_144 (.value(n32bit_decoder_short_15__2));  // open: dp
  // DotMatrix #(.inputtype("select"), .matrixcols(32), .matrixrows(32), .persist(128)) dotmatrix_1: pin names not known; wires that end beside it: dotmatrix_1_p1, dotmatrix_1_p2
  _64x64_display_controller u_64x64_display_controller_1 (
    .clk(clk), .x11(dotmatrix_1_p1), .x21(n64x64_display_controller_1_x21),
    .x12(n64x64_display_controller_1_x12), .x22(n64x64_display_controller_1_x22), .y11(dotmatrix_1_p2),
    .y21(n64x64_display_controller_1_y21), .y12(n64x64_display_controller_1_y12),
    .y22(n64x64_display_controller_1_y22), .x(x), .y(y), .clear(reset_2_out), .state(state),
    .update_frame(update_out));
  // DotMatrix #(.inputtype("select"), .matrixcols(32), .matrixrows(32), .persist(128)) dotmatrix_2: pin names not known; wires that end beside it: n64x64_display_controller_1_x12, n64x64_display_controller_1_y12
  _7_Segment_Display u_7_segment_display_16 (.g(n32bit_decoder_short_16_sign));  // open: f, a, b, e, d, c, dp
  Hex_Digit_Display hex_digit_display_145 (.value(n32bit_decoder_short_16__4));  // open: dp
  _7_Segment_Display u_7_segment_display_17 (.g(n32bit_decoder_short_17_sign));  // open: f, a, b, e, d, c, dp
  Hex_Digit_Display hex_digit_display_146 (.value(n32bit_decoder_short_17__4));  // open: dp
  Hex_Digit_Display hex_digit_display_147 (.value(n32bit_decoder_short_13__5));  // open: dp
  Hex_Digit_Display hex_digit_display_148 (.value(n32bit_decoder_short_13__4_2));  // open: dp
  _32bit_decoder_short u_32bit_decoder_short_13 (
    .sign(n32bit_decoder_short_13_sign), ._4(n32bit_decoder_short_13__4), ._3(n32bit_decoder_short_13__3),
    ._2_2(n32bit_decoder_short_13__2_2), ._1_2(n32bit_decoder_short_13__1_2),
    ._0(n32bit_decoder_short_13__0), .dot(n32bit_decoder_short_13_dot), .in(_31),
    ._1(n32bit_decoder_short_13__1), ._2(n32bit_decoder_short_13__2), ._3_2(n32bit_decoder_short_13__3_2),
    ._4_2(n32bit_decoder_short_13__4_2), ._5(n32bit_decoder_short_13__5));
  Hex_Digit_Display hex_digit_display_149 (.value(n32bit_decoder_short_14__5));  // open: dp
  Hex_Digit_Display hex_digit_display_150 (.value(n32bit_decoder_short_14__4_2));  // open: dp
  _32bit_decoder_short u_32bit_decoder_short_14 (
    .sign(n32bit_decoder_short_14_sign), ._4(n32bit_decoder_short_14__4), ._3(n32bit_decoder_short_14__3),
    ._2_2(n32bit_decoder_short_14__2_2), ._1_2(n32bit_decoder_short_14__1_2),
    ._0(n32bit_decoder_short_14__0), .dot(n32bit_decoder_short_14_dot), .in(_32),
    ._1(n32bit_decoder_short_14__1), ._2(n32bit_decoder_short_14__2), ._3_2(n32bit_decoder_short_14__3_2),
    ._4_2(n32bit_decoder_short_14__4_2), ._5(n32bit_decoder_short_14__5));
  Hex_Digit_Display hex_digit_display_151 (.value(n32bit_decoder_short_15__4_2));  // open: dp
  Hex_Digit_Display hex_digit_display_152 (.value(n32bit_decoder_short_15__5));  // open: dp
  _32bit_decoder_short u_32bit_decoder_short_15 (
    .sign(n32bit_decoder_short_15_sign), ._4(n32bit_decoder_short_15__4), ._3(n32bit_decoder_short_15__3),
    ._2_2(n32bit_decoder_short_15__2_2), ._1_2(n32bit_decoder_short_15__1_2),
    ._0(n32bit_decoder_short_15__0), .dot(n32bit_decoder_short_15_dot), .in(_33),
    ._1(n32bit_decoder_short_15__1), ._2(n32bit_decoder_short_15__2), ._3_2(n32bit_decoder_short_15__3_2),
    ._4_2(n32bit_decoder_short_15__4_2), ._5(n32bit_decoder_short_15__5));
  Hex_Digit_Display hex_digit_display_153 (.value(n32bit_decoder_short_16__2_2));  // open: dp
  Hex_Digit_Display hex_digit_display_154 (.value(n32bit_decoder_short_16__3));  // open: dp
  Hex_Digit_Display hex_digit_display_155 (.value(n32bit_decoder_short_17__3));  // open: dp
  Hex_Digit_Display hex_digit_display_156 (.value(n32bit_decoder_short_17__2_2));  // open: dp
  _7_Segment_Display u_7_segment_display_18 (.g(n32bit_decoder_short_18_sign));  // open: f, a, b, e, d, c, dp
  _7_Segment_Display u_7_segment_display_19 (.g(n32bit_decoder_short_19_sign));  // open: f, a, b, e, d, c, dp
  fp_mult fp_mult_10 (.in1(w_2), .in2(adder_4_out), .out(fp_mult_10_out));
  fp_mult fp_mult_11 (.in1(adder_5_out), .in2(h_2), .out(fp_mult_11_out));
  Hex_Digit_Display hex_digit_display_157 (.value(n32bit_decoder_short_16__0), .dp(n32bit_decoder_short_16_dot));
  Hex_Digit_Display hex_digit_display_158 (.value(n32bit_decoder_short_16__1_2));  // open: dp
  Hex_Digit_Display hex_digit_display_159 (.value(n32bit_decoder_short_17__0), .dp(n32bit_decoder_short_17_dot));
  Hex_Digit_Display hex_digit_display_160 (.value(n32bit_decoder_short_17__1_2));  // open: dp
  Hex_Digit_Display hex_digit_display_161 (.value(n32bit_decoder_short_18__3));  // open: dp
  Hex_Digit_Display hex_digit_display_162 (.value(n32bit_decoder_short_18__4));  // open: dp
  Hex_Digit_Display hex_digit_display_163 (.value(n32bit_decoder_short_19__3));  // open: dp
  Hex_Digit_Display hex_digit_display_164 (.value(n32bit_decoder_short_19__4));  // open: dp
  Hex_Digit_Display hex_digit_display_165 (.value(n32bit_decoder_short_16__1));  // open: dp
  Hex_Digit_Display hex_digit_display_166 (.value(n32bit_decoder_short_16__2));  // open: dp
  Hex_Digit_Display hex_digit_display_167 (.value(n32bit_decoder_short_17__1));  // open: dp
  Hex_Digit_Display hex_digit_display_168 (.value(n32bit_decoder_short_17__2));  // open: dp
  Hex_Digit_Display hex_digit_display_169 (.value(n32bit_decoder_short_18__1_2));  // open: dp
  Hex_Digit_Display hex_digit_display_170 (.value(n32bit_decoder_short_18__2_2));  // open: dp
  Hex_Digit_Display hex_digit_display_171 (.value(n32bit_decoder_short_19__1_2));  // open: dp
  Hex_Digit_Display hex_digit_display_172 (.value(n32bit_decoder_short_19__2_2));  // open: dp
  Negator #(.width(32)) negator_1 (.in(in_1), .out(negator_1_out));
  // DotMatrix #(.inputtype("select"), .matrixcols(32), .matrixrows(32), .persist(128)) dotmatrix_3: pin names not known; wires that end beside it: n64x64_display_controller_1_x21, n64x64_display_controller_1_y21
  // DotMatrix #(.inputtype("select"), .matrixcols(32), .matrixrows(32), .persist(128)) dotmatrix_4: pin names not known; wires that end beside it: n64x64_display_controller_1_x22, n64x64_display_controller_1_y22
  Hex_Digit_Display hex_digit_display_173 (.value(n32bit_decoder_short_16__3_2));  // open: dp
  Hex_Digit_Display hex_digit_display_174 (.value(n32bit_decoder_short_16__4_2));  // open: dp
  Hex_Digit_Display hex_digit_display_175 (.value(n32bit_decoder_short_17__3_2));  // open: dp
  Hex_Digit_Display hex_digit_display_176 (.value(n32bit_decoder_short_17__4_2));  // open: dp
  Hex_Digit_Display hex_digit_display_177 (.value(n32bit_decoder_short_18__1));  // open: dp
  Hex_Digit_Display hex_digit_display_178 (.value(n32bit_decoder_short_18__0), .dp(n32bit_decoder_short_18_dot));
  Hex_Digit_Display hex_digit_display_179 (.value(n32bit_decoder_short_19__0), .dp(n32bit_decoder_short_19_dot));
  Hex_Digit_Display hex_digit_display_180 (.value(n32bit_decoder_short_19__1));  // open: dp
  Hex_Digit_Display hex_digit_display_181 (.value(n32bit_decoder_short_16__5));  // open: dp
  _32bit_decoder_short u_32bit_decoder_short_16 (
    .sign(n32bit_decoder_short_16_sign), ._4(n32bit_decoder_short_16__4), ._3(n32bit_decoder_short_16__3),
    ._2_2(n32bit_decoder_short_16__2_2), ._1_2(n32bit_decoder_short_16__1_2),
    ._0(n32bit_decoder_short_16__0), .dot(n32bit_decoder_short_16_dot), .in(vec4_to_vec3_2_out1),
    ._1(n32bit_decoder_short_16__1), ._2(n32bit_decoder_short_16__2), ._3_2(n32bit_decoder_short_16__3_2),
    ._4_2(n32bit_decoder_short_16__4_2), ._5(n32bit_decoder_short_16__5));
  Hex_Digit_Display hex_digit_display_182 (.value(n32bit_decoder_short_17__5));  // open: dp
  _32bit_decoder_short u_32bit_decoder_short_17 (
    .sign(n32bit_decoder_short_17_sign), ._4(n32bit_decoder_short_17__4), ._3(n32bit_decoder_short_17__3),
    ._2_2(n32bit_decoder_short_17__2_2), ._1_2(n32bit_decoder_short_17__1_2),
    ._0(n32bit_decoder_short_17__0), .dot(n32bit_decoder_short_17_dot), .in(vec4_to_vec3_2_out2),
    ._1(n32bit_decoder_short_17__1), ._2(n32bit_decoder_short_17__2), ._3_2(n32bit_decoder_short_17__3_2),
    ._4_2(n32bit_decoder_short_17__4_2), ._5(n32bit_decoder_short_17__5));
  Hex_Digit_Display hex_digit_display_183 (.value(n32bit_decoder_short_18__2));  // open: dp
  Hex_Digit_Display hex_digit_display_184 (.value(n32bit_decoder_short_18__3_2));  // open: dp
  Hex_Digit_Display hex_digit_display_185 (.value(n32bit_decoder_short_19__2));  // open: dp
  Hex_Digit_Display hex_digit_display_186 (.value(n32bit_decoder_short_19__3_2));  // open: dp
  _7_Segment_Display u_7_segment_display_20 (.g(n32bit_decoder_short_20_sign));  // open: f, a, b, e, d, c, dp
  Hex_Digit_Display hex_digit_display_187 (.value(n32bit_decoder_short_18__5));  // open: dp
  Hex_Digit_Display hex_digit_display_188 (.value(n32bit_decoder_short_18__4_2));  // open: dp
  Hex_Digit_Display hex_digit_display_189 (.value(n32bit_decoder_short_19__4_2));  // open: dp
  Hex_Digit_Display hex_digit_display_190 (.value(n32bit_decoder_short_19__5));  // open: dp
  Hex_Digit_Display hex_digit_display_191 (.value(n32bit_decoder_short_20__4));  // open: dp
  _32bit_decoder_short u_32bit_decoder_short_18 (
    .sign(n32bit_decoder_short_18_sign), ._4(n32bit_decoder_short_18__4), ._3(n32bit_decoder_short_18__3),
    ._2_2(n32bit_decoder_short_18__2_2), ._1_2(n32bit_decoder_short_18__1_2),
    ._0(n32bit_decoder_short_18__0), .dot(n32bit_decoder_short_18_dot), .in(fp_mult_10_out),
    ._1(n32bit_decoder_short_18__1), ._2(n32bit_decoder_short_18__2), ._3_2(n32bit_decoder_short_18__3_2),
    ._4_2(n32bit_decoder_short_18__4_2), ._5(n32bit_decoder_short_18__5));
  _32bit_decoder_short u_32bit_decoder_short_19 (
    .sign(n32bit_decoder_short_19_sign), ._4(n32bit_decoder_short_19__4), ._3(n32bit_decoder_short_19__3),
    ._2_2(n32bit_decoder_short_19__2_2), ._1_2(n32bit_decoder_short_19__1_2),
    ._0(n32bit_decoder_short_19__0), .dot(n32bit_decoder_short_19_dot), .in(fp_mult_11_out),
    ._1(n32bit_decoder_short_19__1), ._2(n32bit_decoder_short_19__2), ._3_2(n32bit_decoder_short_19__3_2),
    ._4_2(n32bit_decoder_short_19__4_2), ._5(n32bit_decoder_short_19__5));
  Hex_Digit_Display hex_digit_display_192 (.value(n32bit_decoder_short_20__3));  // open: dp
  Hex_Digit_Display hex_digit_display_193 (.value(n32bit_decoder_short_20__2_2));  // open: dp
  Hex_Digit_Display hex_digit_display_194 (.value(n32bit_decoder_short_20__0), .dp(n32bit_decoder_short_20_dot));
  Hex_Digit_Display hex_digit_display_195 (.value(n32bit_decoder_short_20__1_2));  // open: dp
  fp_mult fp_mult_12 (.in1(32'h3e80000), .in2(32'hffff0000), .out(fp_mult_12_out));
  Hex_Digit_Display hex_digit_display_196 (.value(n32bit_decoder_short_20__2));  // open: dp
  Hex_Digit_Display hex_digit_display_197 (.value(n32bit_decoder_short_20__1));  // open: dp
  fp_mult fp_mult_13 (.in1(f_aspect_ratio), .in2(f_fov_rad), .out(fp_mult_13_out));
  fp_div fp_div_10 (.in1(32'h3e80000), .in2(subtractor_3_out), .out(fp_div_10_out));
  fp_mult fp_mult_14 (.in1(fp_mult_12_out), .in2(32'h1999), .out(fp_mult_14_out));
  fp_div fp_div_11 (.in1(fp_mult_14_out), .in2(subtractor_3_out), .out(fp_div_11_out));
  Subtractor #(.width(32)) subtractor_3 (.a(32'h3e80000), .b(32'h1999), .out(subtractor_3_out));  // open: bin, bout
  Hex_Digit_Display hex_digit_display_198 (.value(n32bit_decoder_short_20__3_2));  // open: dp
  Hex_Digit_Display hex_digit_display_199 (.value(n32bit_decoder_short_20__4_2));  // open: dp
  Hex_Digit_Display hex_digit_display_200 (.value(n32bit_decoder_short_20__5));  // open: dp
  _32bit_decoder_short u_32bit_decoder_short_20 (
    .sign(n32bit_decoder_short_20_sign), ._4(n32bit_decoder_short_20__4), ._3(n32bit_decoder_short_20__3),
    ._2_2(n32bit_decoder_short_20__2_2), ._1_2(n32bit_decoder_short_20__1_2),
    ._0(n32bit_decoder_short_20__0), .dot(n32bit_decoder_short_20_dot), .in(negator_1_out),
    ._1(n32bit_decoder_short_20__1), ._2(n32bit_decoder_short_20__2), ._3_2(n32bit_decoder_short_20__3_2),
    ._4_2(n32bit_decoder_short_20__4_2), ._5(n32bit_decoder_short_20__5));
  // matrix_mult_4x4 matrix_mult_4x4_3: pin names not known
  matrix_mult_4x4 matrix_mult_4x4_4 (
    .in_1(in_13), .in_5(in_15), .in_9(in_17), .in_13(32'h10000), .in_17(fp_mult_13_out), .in_22(f_fov_rad),
    .in_27(fp_div_10_out), .in_28(fp_div_11_out), .in_31(32'h10000), .out11(matrix_mult_4x4_4_out11),
    .out12(matrix_mult_4x4_4_out12), .out13(matrix_mult_4x4_4_out13), .out14(matrix_mult_4x4_4_out14));  // open: in_2, in_3, in_4, in_6, in_7, in_8, in_10, in_11, in_12, in_14, in_15, in_16, in_18, in_19, in_20, in_21, in_23, in_24, in_25, in_26, in_29, in_30, in_32, out21, out31, out41, out22, out32, out42, out23, out33, out43, out24, out34, out44
  vec4_to_vec3 vec4_to_vec3_3 (
    .in1(matrix_mult_4x4_4_out11), .in2(matrix_mult_4x4_4_out12), .in3(matrix_mult_4x4_4_out13),
    .in4(matrix_mult_4x4_4_out14), .out1(vec4_to_vec3_3_out1), .out2(vec4_to_vec3_3_out2),
    .out3(vec4_to_vec3_3_out3));
  // vec4_to_vec3 vec4_to_vec3_4: pin names not known
  _7_Segment_Display u_7_segment_display_21 (.g(n32bit_decoder_short_21_sign));  // open: f, a, b, e, d, c, dp
  Hex_Digit_Display hex_digit_display_201 (.value(n32bit_decoder_short_21__4));  // open: dp
  _7_Segment_Display u_7_segment_display_22 (.g(n32bit_decoder_short_22_sign));  // open: f, a, b, e, d, c, dp
  Hex_Digit_Display hex_digit_display_202 (.value(n32bit_decoder_short_22__4));  // open: dp
  // matrix_mult_sub_4 matrix_mult_sub_4_1: pin names not known
  Hex_Digit_Display hex_digit_display_203 (.value(n32bit_decoder_short_21__3));  // open: dp
  Hex_Digit_Display hex_digit_display_204 (.value(n32bit_decoder_short_21__2_2));  // open: dp
  Hex_Digit_Display hex_digit_display_205 (.value(n32bit_decoder_short_22__3));  // open: dp
  Hex_Digit_Display hex_digit_display_206 (.value(n32bit_decoder_short_22__2_2));  // open: dp
  Hex_Digit_Display hex_digit_display_207 (.value(n32bit_decoder_short_21__0), .dp(n32bit_decoder_short_21_dot));
  Hex_Digit_Display hex_digit_display_208 (.value(n32bit_decoder_short_21__1_2));  // open: dp
  Hex_Digit_Display hex_digit_display_209 (.value(n32bit_decoder_short_22__0), .dp(n32bit_decoder_short_22_dot));
  Hex_Digit_Display hex_digit_display_210 (.value(n32bit_decoder_short_22__1_2));  // open: dp
  Hex_Digit_Display hex_digit_display_211 (.value(n32bit_decoder_short_21__1));  // open: dp
  Hex_Digit_Display hex_digit_display_212 (.value(n32bit_decoder_short_21__2));  // open: dp
  Hex_Digit_Display hex_digit_display_213 (.value(n32bit_decoder_short_22__1));  // open: dp
  Hex_Digit_Display hex_digit_display_214 (.value(n32bit_decoder_short_22__2));  // open: dp
  Hex_Digit_Display hex_digit_display_215 (.value(n32bit_decoder_short_21__3_2));  // open: dp
  Hex_Digit_Display hex_digit_display_216 (.value(n32bit_decoder_short_21__4_2));  // open: dp
  Hex_Digit_Display hex_digit_display_217 (.value(n32bit_decoder_short_22__3_2));  // open: dp
  Hex_Digit_Display hex_digit_display_218 (.value(n32bit_decoder_short_22__4_2));  // open: dp
  Hex_Digit_Display hex_digit_display_219 (.value(n32bit_decoder_short_21__5));  // open: dp
  _32bit_decoder_short u_32bit_decoder_short_21 (
    .sign(n32bit_decoder_short_21_sign), ._4(n32bit_decoder_short_21__4), ._3(n32bit_decoder_short_21__3),
    ._2_2(n32bit_decoder_short_21__2_2), ._1_2(n32bit_decoder_short_21__1_2),
    ._0(n32bit_decoder_short_21__0), .dot(n32bit_decoder_short_21_dot), .in(vec4_to_vec3_3_out1),
    ._1(n32bit_decoder_short_21__1), ._2(n32bit_decoder_short_21__2), ._3_2(n32bit_decoder_short_21__3_2),
    ._4_2(n32bit_decoder_short_21__4_2), ._5(n32bit_decoder_short_21__5));
  Hex_Digit_Display hex_digit_display_220 (.value(n32bit_decoder_short_22__5));  // open: dp
  _32bit_decoder_short u_32bit_decoder_short_22 (
    .sign(n32bit_decoder_short_22_sign), ._4(n32bit_decoder_short_22__4), ._3(n32bit_decoder_short_22__3),
    ._2_2(n32bit_decoder_short_22__2_2), ._1_2(n32bit_decoder_short_22__1_2),
    ._0(n32bit_decoder_short_22__0), .dot(n32bit_decoder_short_22_dot), .in(vec4_to_vec3_3_out2),
    ._1(n32bit_decoder_short_22__1), ._2(n32bit_decoder_short_22__2), ._3_2(n32bit_decoder_short_22__3_2),
    ._4_2(n32bit_decoder_short_22__4_2), ._5(n32bit_decoder_short_22__5));

  // Other names for the same wires on the sheet: R1_12[31:0] = R1_11; R1_13[31:0] = R1_11; R1_21[31:0] = R1_11;
  //   R1_22[31:0] = R1_11; R1_23[31:0] = R1_11; R1_31[31:0] = R1_11; R1_32[31:0] = R1_11; R1_33[31:0] = R1_11;
  //   R2_12[31:0] = R2_11; R2_13[31:0] = R2_11; R2_21[31:0] = R2_11; R2_22[31:0] = R2_11; R2_23[31:0] = R2_11;
  //   R2_31[31:0] = R2_11; R2_32[31:0] = R2_11; R2_33[31:0] = R2_11

  // Notes on the sheet:
  //   in_16: pull=down
  //   in_15: pull=down
  //   in_11: pull=down
  //   in_13: pull=down
  //   in_1: pull=down
  //   Load_sample: pull=down
  //   in_9: pull=down
  //   in_14: pull=down
  //   in_12: pull=down
  //   in_17: pull=down
  //   in_10: pull=down
  //   contents of rom_1 (hex, n*v repeats v):
  //   10000 10000 10000 13*0 10000 10000 10000 13*0 10000 10000 10000 13*0 10000 16*0 10000 16*0 10000
  //   13*0 1000 15*0 1000 15*0 1000 15*0 11000 11000 11000
  //   matrix couter
  //   projection matrix
endmodule

module fp_to_int (
  input  [31:0] in,
  output [31:0] out
);

  Shifter #(.width(32), .shift("lr")) shifter_1 (.in(in), .\dist (5'b10000), .out(out));

  // Notes on the sheet:
  //   in: pull=down
  //   out: pull=down
endmodule

module _64x64_display_controller (
  input  [5:0] y,
  input  [5:0] x,
  input  state,
  input  clear,
  input  update_frame,
  input  clk,
  output [31:0] x12,
  output [31:0] x22,
  output [31:0] x11,
  output [31:0] x21,
  output [31:0] y12,
  output [31:0] y22,
  output [31:0] y11,
  output [31:0] y21
);

  wire and_1_out, and_2_out, and_3_out, counter_1_carry, counter_2_carry, multiplexer_1_out,
       multiplexer_2_out, multiplexer_3_out, multiplexer_6_out, not_1_out, not_2_out, not_3_out, not_4_out,
       not_5_out, not_6_out, or_1_out, s_r_ff_1_q, s_r_ff_2_q, s_r_ff_3_q, s_r_ff_4_q, s_r_ff_5_q;
  wire [5:0] counter_2_q, multiplexer_5_out;
  wire [31:0] decoder_1_out0, decoder_2_out0, multiplexer_7_out, multiplexer_8_out, or_2_out,
       pull_resistor_2_node, ram_1_data, ram_2_data, ram_3_data, ram_4_data;

  Register #(.width(6)) register_1 ();  // open: D, en, Q, clk, clr
  not not_1 (not_1_out, update_frame);
  and and_1 (and_1_out, update_frame, s_r_ff_1_q);
  S_R_Flip_Flop s_r_ff_1 (.Q(s_r_ff_1_q), .preset(not_1_out), .reset(s_r_ff_2_q));  // open: S, clk, R, Qn, en
  S_R_Flip_Flop s_r_ff_2 (.Q(s_r_ff_2_q), .preset(and_1_out), .reset(s_r_ff_4_q));  // open: S, clk, R, Qn, en
  Decoder #(.select(5)) decoder_1 (
    .out0(decoder_1_out0[0]), .out1(decoder_1_out0[1]), .out2(decoder_1_out0[2]), .out3(decoder_1_out0[3]),
    .out4(decoder_1_out0[4]), .out5(decoder_1_out0[5]), .out6(decoder_1_out0[6]), .out7(decoder_1_out0[7]),
    .out8(decoder_1_out0[8]), .out9(decoder_1_out0[9]), .out10(decoder_1_out0[10]),
    .out11(decoder_1_out0[11]), .out12(decoder_1_out0[12]), .out13(decoder_1_out0[13]),
    .out14(decoder_1_out0[14]), .out15(decoder_1_out0[15]), .out16(decoder_1_out0[16]),
    .out17(decoder_1_out0[17]), .out18(decoder_1_out0[18]), .out19(decoder_1_out0[19]),
    .out20(decoder_1_out0[20]), .out21(decoder_1_out0[21]), .out22(decoder_1_out0[22]),
    .out23(decoder_1_out0[23]), .out24(decoder_1_out0[24]), .out25(decoder_1_out0[25]),
    .out26(decoder_1_out0[26]), .out27(decoder_1_out0[27]), .out28(decoder_1_out0[28]),
    .out29(decoder_1_out0[29]), .out30(decoder_1_out0[30]), .out31(decoder_1_out0[31]), .sel(x[4:0]),
    .en(state));
  and and_2 (and_2_out, s_r_ff_2_q, s_r_ff_5_q);
  Pull_Resistor pull_resistor_1 (.node(decoder_1_out0));
  S_R_Flip_Flop s_r_ff_3 (.S(and_2_out), .clk(clk), .R(s_r_ff_4_q), .Q(s_r_ff_3_q));  // open: Qn, preset, reset, en
  Multiplexer #(.enable("false")) multiplexer_1 (.in0(state), .in1(1'b0), .out(multiplexer_1_out), .sel(s_r_ff_3_q));
  Counter #(.width(6), .max('h3f)) counter_1 (
    .carry(counter_1_carry), .clk(and_3_out));  // open: load, D, count, Q, clr
  and and_3 (and_3_out, clk, s_r_ff_3_q);
  Pull_Resistor pull_resistor_2 (.node(pull_resistor_2_node));
  not not_2 (not_2_out, x[5]);
  or or_1 (or_1_out, clear, clear);
  S_R_Flip_Flop s_r_ff_4 (.Q(s_r_ff_4_q), .preset(counter_1_carry), .reset(clk));  // open: S, clk, R, Qn, en
  S_R_Flip_Flop s_r_ff_5 (.Q(s_r_ff_5_q), .preset(counter_2_carry), .reset(clk));  // open: S, clk, R, Qn, en
  assign or_2_out = pull_resistor_2_node | decoder_1_out0;  // OR_Gate or_2, 32 bits wide
  Multiplexer #(.enable("false")) multiplexer_2 (.in0(x[5]), .in1(1'b1), .out(multiplexer_2_out), .sel(s_r_ff_3_q));
  Multiplexer #(.enable("false")) multiplexer_3 (
    .in0(not_2_out), .in1(1'b1), .out(multiplexer_3_out), .sel(s_r_ff_3_q));
  Multiplexer #(.width(32)) multiplexer_4 (
    .in0(ram_3_data), .in1(ram_1_data), .out(pull_resistor_2_node), .sel(multiplexer_3_out), .en(not_3_out));
  Multiplexer #(.width(6), .enable("false")) multiplexer_5 (
    .in0(y), .in1(counter_2_q), .out(multiplexer_5_out), .sel(s_r_ff_3_q));
  Counter #(.width(6), .max('h3f)) counter_2 (
    .Q(counter_2_q), .carry(counter_2_carry), .clk(clk));  // open: load, D, count, clr
  not not_3 (not_3_out, s_r_ff_3_q);
  Decoder #(.select(5), .enable("false")) decoder_2 (
    .out0(decoder_2_out0[0]), .out1(decoder_2_out0[1]), .out2(decoder_2_out0[2]), .out3(decoder_2_out0[3]),
    .out4(decoder_2_out0[4]), .out5(decoder_2_out0[5]), .out6(decoder_2_out0[6]), .out7(decoder_2_out0[7]),
    .out8(decoder_2_out0[8]), .out9(decoder_2_out0[9]), .out10(decoder_2_out0[10]),
    .out11(decoder_2_out0[11]), .out12(decoder_2_out0[12]), .out13(decoder_2_out0[13]),
    .out14(decoder_2_out0[14]), .out15(decoder_2_out0[15]), .out16(decoder_2_out0[16]),
    .out17(decoder_2_out0[17]), .out18(decoder_2_out0[18]), .out19(decoder_2_out0[19]),
    .out20(decoder_2_out0[20]), .out21(decoder_2_out0[21]), .out22(decoder_2_out0[22]),
    .out23(decoder_2_out0[23]), .out24(decoder_2_out0[24]), .out25(decoder_2_out0[25]),
    .out26(decoder_2_out0[26]), .out27(decoder_2_out0[27]), .out28(decoder_2_out0[28]),
    .out29(decoder_2_out0[29]), .out30(decoder_2_out0[30]), .out31(decoder_2_out0[31]), .sel(counter_2_q[4:0]));
  Multiplexer #(.enable("false")) multiplexer_6 (.in0(state), .in1(1'b1), .out(multiplexer_6_out), .sel(s_r_ff_3_q));
  not not_4 (not_4_out, s_r_ff_3_q);
  RAM #(.addrWidth(6), .dataWidth(32), .bus("separate")) ram_1 (
    .addr(multiplexer_5_out), .din(or_2_out), .data(ram_1_data), .str(multiplexer_1_out),
    .sel(multiplexer_3_out), .clk(clk), .ld(multiplexer_6_out), .clr(or_1_out));
  RAM #(.addrWidth(6), .dataWidth(32), .bus("separate")) ram_2 (
    .addr(counter_2_q), .din(ram_1_data), .data(ram_2_data), .str(s_r_ff_3_q), .clk(clk), .ld(not_4_out));  // open: sel, clr
  not not_5 (not_5_out, s_r_ff_3_q);
  RAM #(.addrWidth(6), .dataWidth(32), .bus("separate")) ram_3 (
    .addr(multiplexer_5_out), .din(or_2_out), .data(ram_3_data), .str(multiplexer_1_out),
    .sel(multiplexer_2_out), .clk(clk), .ld(multiplexer_6_out), .clr(or_1_out));
  RAM #(.addrWidth(6), .dataWidth(32), .bus("separate")) ram_4 (
    .addr(counter_2_q), .din(ram_3_data), .data(ram_4_data), .str(s_r_ff_3_q), .clk(clk), .ld(not_5_out));  // open: sel, clr
  Multiplexer #(.width(32), .enable("false")) multiplexer_7 (
    .in0(ram_4_data), .in1(ram_3_data), .out(multiplexer_7_out), .sel(s_r_ff_3_q));
  Multiplexer #(.width(32), .enable("false")) multiplexer_8 (
    .in0(ram_2_data), .in1(ram_1_data), .out(multiplexer_8_out), .sel(s_r_ff_3_q));
  not not_6 (not_6_out, counter_2_q[5]);
  Register #(.width(32)) register_2 (.D(multiplexer_7_out), .en(not_6_out), .Q(x22), .clk(clk), .clr(counter_2_q[5]));
  Register #(.width(32)) register_3 (.D(multiplexer_7_out), .en(counter_2_q[5]), .Q(x21), .clk(clk), .clr(not_6_out));
  Register #(.width(32)) register_4 (.D(decoder_2_out0), .en(not_6_out), .Q(y12), .clk(clk), .clr(counter_2_q[5]));
  Register #(.width(32)) register_5 (.D(decoder_2_out0), .en(counter_2_q[5]), .Q(y11), .clk(clk), .clr(not_6_out));
  Register #(.width(32)) register_6 (.D(multiplexer_8_out), .en(not_6_out), .Q(x12), .clk(clk), .clr(counter_2_q[5]));
  Register #(.width(32)) register_7 (.D(multiplexer_8_out), .en(counter_2_q[5]), .Q(x11), .clk(clk), .clr(not_6_out));
  Register #(.width(32)) register_8 (.D(decoder_2_out0), .en(not_6_out), .Q(y22), .clk(clk), .clr(counter_2_q[5]));
  Register #(.width(32)) register_9 (.D(decoder_2_out0), .en(counter_2_q[5]), .Q(y21), .clk(clk), .clr(not_6_out));

  // Notes on the sheet:
  //   y: pull=down
  //   update_frame: pull=down
  //   state: pull=down
  //   y11: pull=down
  //   x22: pull=down
  //   x11: pull=down
  //   x21: pull=down
  //   x: pull=down
  //   clear: pull=down
  //   clk: pull=down
  //   y12: pull=down
  //   y21: pull=down
  //   y22: pull=down
  //   x12: pull=down
  //   detect sig (async)
  //   sync async sig to mian counter
  //   sync async sig to clk
endmodule

module int_to_fp (
  input  [31:0] in,
  output [31:0] out
);

  Shifter #(.width(32)) shifter_1 (.in(in), .\dist (5'b10000), .out(out));

  // Notes on the sheet:
  //   in: pull=down
  //   out: pull=down
endmodule

module DDA_test (
  input  IN,
  input  in_2,
  input  x1,
  input  x2,
  input  [31:0] x2_2,
  input  [31:0] x1_2,
  input  [31:0] y2,
  input  [31:0] y1,
  output [31:0] out_y,
  output [3:0] status,
  output [31:0] out_x,
  output out_12,
  output out_13
);

  wire and_1_out, and_2_out, and_3_out, and_4_out, button_1_out, mem, nand_1_out, nand_2_out, nand_3_out,
       nand_4_out, nand_6_out, nand_7_out, nand_8_out, nand_10_out, nand_11_out, nand_12_out, nand_14_out,
       nand_15_out, nand_17_out, nand_18_out, nand_19_out, not_1_out;
  wire [1:0] comparator_1_gt, mission, or_1_out, state;
  wire [1:1] comparator_1_lt;
  wire [31:0] dx, dy, fp_abs_1_abs, fp_abs_2_abs, out_x_t, out_y_t, steps_count, x, x1_t, x2_t, x_dx, x_step,
       y, y1_t, y2_t, y_dy, y_step;

  Register #(.width(32)) register_1 (.D(x2_2), .en(mem), .Q(x2_t), .clk(IN));  // open: clr
  Register #(.width(32)) register_2 (.D(x1_2), .en(mem), .Q(x1_t), .clk(IN));  // open: clr
  Register #(.width(32)) register_3 (.D(y2), .en(mem), .Q(y2_t), .clk(IN));  // open: clr
  Register #(.width(32)) register_4 (.D(y1), .en(mem), .Q(y1_t), .clk(IN));  // open: clr
  and and_1 (and_1_out, ~mission[0], mission[1]);  // AND_Gate
  and and_2 (and_2_out, mission[0], mission[1]);
  and and_3 (and_3_out, mission[0], ~mission[1]);  // AND_Gate
  assign x = and_1_out ? x1_t : 32'bz;  // Controlled_Buffer controlled_buffer_1
  assign x = and_2_out ? x2_t : 32'bz;  // Controlled_Buffer controlled_buffer_2
  assign x = and_3_out ? x_dx : 32'bz;  // Controlled_Buffer controlled_buffer_3
  assign y = and_1_out ? y1_t : 32'bz;  // Controlled_Buffer controlled_buffer_4
  assign y = and_2_out ? y2_t : 32'bz;  // Controlled_Buffer controlled_buffer_5
  assign y = and_3_out ? y_dy : 32'bz;  // Controlled_Buffer controlled_buffer_6
  fp_abs fp_abs_1 (.in(dx), .abs(fp_abs_1_abs));
  Subtractor #(.width(32)) subtractor_1 (.a(x2_t), .b(x1_t), .out(dx));  // open: bin, bout
  Subtractor #(.width(32)) subtractor_2 (.a(y2_t), .b(y1_t), .out(dy));  // open: bin, bout
  fp_abs fp_abs_2 (.in(dy), .abs(fp_abs_2_abs));
  Adder #(.width(32)) adder_1 (.a(out_x_t), .b(x_step), .out(x_dx));  // open: cin, cout
  Adder #(.width(32)) adder_2 (.a(out_y_t), .b(y_step), .out(y_dy));  // open: cin, cout
  fp_round_ones fp_round_ones_1 (.num(out_x_t), .out(out_y));
  fp_round_ones fp_round_ones_2 (.num(out_y_t), .out(out_x));
  Comparator #(.width(32)) comparator_1 (
    .a(fp_abs_1_abs), .b(fp_abs_2_abs), .gt(comparator_1_gt[0]), .eq(comparator_1_gt[1]),
    .lt(comparator_1_lt[1]));
  Register #(.width(32)) register_5 (.D(x), .Q(out_x_t), .clk(IN), .clr(button_1_out));  // open: en
  Register #(.width(32)) register_6 (.D(y), .Q(out_y_t), .clk(IN), .clr(button_1_out));  // open: en
  assign or_1_out = comparator_1_gt | {2{comparator_1_lt[1]}};  // OR_Gate or_1, 2 bits wide
  fp_div fp_div_1 (.in1(dx), .in2(steps_count), .out(x_step));
  fp_div fp_div_2 (.in1(dy), .in2(steps_count), .out(y_step));
  Button button_1 (.out(button_1_out));
  Multiplexer #(.select(2), .width(32), .enable("false")) multiplexer_1 (
    .in1(fp_abs_1_abs), .in2(fp_abs_1_abs), .in3(fp_abs_2_abs), .out(steps_count), .sel(or_1_out));  // open: in0
  nand nand_1 (nand_1_out, ~state[0], 1'b0);  // NAND_Gate
  nand nand_2 (nand_2_out, 1'b0, 1'b0);
  nand nand_3 (nand_3_out, ~state[0], ~1'b0);  // NAND_Gate
  nand nand_4 (nand_4_out, state[0], state[1]);
  nand nand_5 (mission[0], nand_4_out, nand_6_out, nand_7_out);
  nand nand_6 (nand_6_out, state[1], 1'b0);
  nand nand_7 (nand_7_out, state[0], 1'b0);
  nand nand_8 (nand_8_out, ~state[0], state[1], 1'b0);  // NAND_Gate
  nand nand_9 (mission[1], nand_8_out, nand_10_out);
  nand nand_10 (nand_10_out, state[0], ~state[1], 1'b0);  // NAND_Gate
  nand nand_11 (nand_11_out, ~state[0], ~state[1], 1'b0);  // NAND_Gate
  nand nand_12 (nand_12_out, 1'b0, 1'b0);
  nand nand_13 (out_12, nand_11_out, nand_12_out, nand_14_out);
  nand nand_14 (nand_14_out, state[0], state[1], ~1'b0);  // NAND_Gate
  nand nand_15 (nand_15_out, 1'b0, 1'b0);
  nand nand_16 (out_13, nand_15_out, not_1_out);
  not not_1 (not_1_out, state[0]);
  and and_4 (and_4_out, 1'b0, state[1]);
  nand nand_17 (nand_17_out, ~state[1], 1'b0);  // NAND_Gate
  nand nand_18 (nand_18_out, nand_1_out, nand_2_out);
  nand nand_19 (nand_19_out, 1'b0, nand_3_out);
  J_K_Flip_Flop j_k_ff_1 (.J(and_4_out), .clk(IN), .K(nand_17_out), .Q(state[0]));  // open: Qn, preset, en, reset
  J_K_Flip_Flop j_k_ff_2 (.J(nand_18_out), .clk(IN), .K(nand_19_out), .Q(state[1]));  // open: Qn, preset, en, reset
  and and_5 (status[1], ~1'b0, 1'b0);  // AND_Gate
  Hex_Digit_Display hex_digit_display_1 (.value({2'b00, status[1], 1'b0}));  // open: dp

  assign {status[3:2], status[0]} = 3'b000;

  // Other names for the same wires on the sheet: clk = IN; done = out_13; new_data = in_2; set_point = out_12

  // Notes on the sheet:
  //   x1: pull=down
  //   x2: pull=down
  //   out_13: pull=up
  //   out_12: pull=up
  //   REG LOADER
  //   OUT
  //   MATH
  //   OUT REG
  //   MAIN LOGIC
  //   STATE MACHINE
  //   00 - halt do nothg
  //   01 - load x1y1
  //   10 - increment by step
  //   11 - load x2y2
  //   STATUS
  //   0: halt
  //   1: run
  //   2: error
endmodule
