// Logisim project tablica_sin_i_cos.circ as structural Verilog: 1 circuit, main circuit sin&co
module sin_co (
  input  [31:0] in_1,
  output [31:0] sin,
  output [31:0] cos
);

  ROM #(.addrWidth(16), .dataWidth(32)) rom_1 (.addr(in_1[31:16]), .data(cos));  // open: sel
  ROM #(.addrWidth(16), .dataWidth(32)) rom_2 (.addr(in_1[31:16]), .data(sin));  // open: sel

  // Notes on the sheet:
  //   in_1: pull=down
  //   sin: pull=down
  //   cos: pull=down
  //   COSINUS
  //   SINUS
  //   contents of rom_1 (hex, n*v repeats v):
  //   10000 fff2 ffd8 ffa4 ff62 ff06 fe97 fe14 fd84 fcd9 fc1b fb4a fa64 f972 f865 f745 f617 f4d0 f37b f20c
  //   f090 ef00 ed5c eba5 e9db e803 e617 e418 e205 dfe5 ddb2 db71 d916 d6b5 d439 d1b7 cf1a cc71 c9ba c6f0
  //   c418 c134 be3b bb3d b824 b504 b1d7 ae97 ab4a a7f6 a48e a119 9d9e 9a0f 967a 92d7 8f27 8b6a 87a7 83d7
  //   8000 7c1b 7831 7439 703a 6c2f 681d 6404 5fe5 5bc0 578d 535a 4f1a 4ada 468d 4240 3ded 3999 3538 30d8
  //   2c71 2809 23a2 1f34 1ac0 1652 11de d63 8ef 47a
  //   contents of rom_2 (hex, n*v repeats v):
  //   0 47a 8ef d63 11de 1652 1ac0 1f34 23a2 2809 2c71 30d8 3538 3999 3ded 4240 468d 4ada 4f1a 535a 578d
  //   5bc0 5fe5 6404 681d 6c2f 703a 7439 7831 7c1b 8000 83d7 87a7 8b6a 8f27 92d7 967a 9a0f 9d9e a119 a48e
  //   a7f6 ab4a ae97 b1d7 b504 b824 bb3d be3b c134 c418 c6f0 c9ba cc71 cf1a d1b7 d439 d6b5 d916 db71 ddb2
  //   dfe5 e205 e418 e617 e803 e9db eba5 ed5c ef00 f090 f20c f37b f4d0 f617 f745 f865 f972 fa64 fb4a fc1b
  //   fcd9 fd84 fe14 fe97 ff06 ff62 ffa4 ffd8 fff2 10000
endmodule
